// Logisim project ALU.circ as structural Verilog: 8 circuits, main circuit main
module main (
  input  [7:0] Left_Input,
  input  [7:0] Right_Input,
  input  Clock,
  input  [1:0] in_4,
  input  R_W,
  output [7:0] A_out_Output,
  output Overflow,
  output Zero
);

  wire and_1_out, and_2_out, and_3_out, Left__0_2, Left__1_2, Left__2_2, Left__3_2, Left__4_2, Left__5_2,
       Left__6_2, Left__7_2, n4_bit_multiplier_1_zero, n8_bit_adder_subtractor_1_overflow,
       n8_bit_adder_subtractor_1_zero, n8_bit_condition_3_out_14, n8_bit_condition_3_out_15,
       n8_bit_condition_3_out_16, n8_bit_condition_3_out_17, n8_bit_condition_4_out_14,
       n8_bit_condition_4_out_15, n8_bit_condition_4_out_16, n8_bit_condition_4_out_17, n8_bit_or_gate_1__0,
       n8_bit_or_gate_1__1, n8_bit_or_gate_1__2, n8_bit_or_gate_1__3, n8_bit_or_gate_1__4,
       n8_bit_or_gate_1__5, n8_bit_or_gate_1__6, n8_bit_or_gate_1__7, not_1_out, or_1_out, Right__0_2,
       Right__1_2, Right__2_2, Right__3_2, Right__4_2, Right__5_2, Right__6_2, Right__7_2;
  wire [3:0] n8_bit_condition_3_out_10, n8_bit_condition_4_out_10;
  wire [7:0] n4_bit_multiplier_1_out_4, n8_bit_adder_subtractor_1_result, n8_bit_condition_1_out_10,
       n8_bit_condition_2_out_10;

  not not_1 (not_1_out, in_4[1]);
  and and_1 (and_1_out, in_4[0], not_1_out);
  _8_bit_Condition_Gate u_8_bit_condition_1 (
    .Condition(not_1_out), .in_2(Left__0_2), .in_3(Left__1_2), .in_4(Left__2_2), .in_5(Left__3_2),
    .in_6(Left__4_2), .in_7(Left__5_2), .in_8(Left__6_2), .in_9(Left__7_2),
    .out_10(n8_bit_condition_1_out_10[0]), .out_11(n8_bit_condition_1_out_10[1]),
    .out_12(n8_bit_condition_1_out_10[2]), .out_13(n8_bit_condition_1_out_10[3]),
    .out_14(n8_bit_condition_1_out_10[4]), .out_15(n8_bit_condition_1_out_10[5]),
    .out_16(n8_bit_condition_1_out_10[6]), .out_17(n8_bit_condition_1_out_10[7]));
  _8_bit_Adder_Subtractor u_8_bit_adder_subtractor_1 (
    .Left_Input(n8_bit_condition_1_out_10), .Right_Input(n8_bit_condition_2_out_10),
    .Overflow(n8_bit_adder_subtractor_1_overflow), .Add_Subtract(and_1_out),
    .Result(n8_bit_adder_subtractor_1_result), .Zero(n8_bit_adder_subtractor_1_zero));
  Register Left (
    .Clock(Clock), .R_W(R_W), ._7(Left_Input[7]), ._6(Left_Input[6]), ._5(Left_Input[5]), ._4(Left_Input[4]),
    ._3(Left_Input[3]), ._2(Left_Input[2]), ._1(Left_Input[1]), ._0(Left_Input[0]), ._7_2(Left__7_2),
    ._6_2(Left__6_2), ._5_2(Left__5_2), ._4_2(Left__4_2), ._3_2(Left__3_2), ._2_2(Left__2_2),
    ._1_2(Left__1_2), ._0_2(Left__0_2));
  _8_bit_Condition_Gate u_8_bit_condition_2 (
    .Condition(not_1_out), .in_2(Right__0_2), .in_3(Right__1_2), .in_4(Right__2_2), .in_5(Right__3_2),
    .in_6(Right__4_2), .in_7(Right__5_2), .in_8(Right__6_2), .in_9(Right__7_2),
    .out_10(n8_bit_condition_2_out_10[0]), .out_11(n8_bit_condition_2_out_10[1]),
    .out_12(n8_bit_condition_2_out_10[2]), .out_13(n8_bit_condition_2_out_10[3]),
    .out_14(n8_bit_condition_2_out_10[4]), .out_15(n8_bit_condition_2_out_10[5]),
    .out_16(n8_bit_condition_2_out_10[6]), .out_17(n8_bit_condition_2_out_10[7]));
  and and_2 (and_2_out, n8_bit_adder_subtractor_1_zero, not_1_out);
  _8_bit_Condition_Gate u_8_bit_condition_3 (
    .Condition(in_4[1]), .in_2(Left__0_2), .in_3(Left__1_2), .in_4(Left__2_2), .in_5(Left__3_2),
    .in_6(Left__4_2), .in_7(Left__5_2), .in_8(Left__6_2), .in_9(Left__7_2),
    .out_10(n8_bit_condition_3_out_10[0]), .out_11(n8_bit_condition_3_out_10[1]),
    .out_12(n8_bit_condition_3_out_10[2]), .out_13(n8_bit_condition_3_out_10[3]),
    .out_14(n8_bit_condition_3_out_14), .out_15(n8_bit_condition_3_out_15),
    .out_16(n8_bit_condition_3_out_16), .out_17(n8_bit_condition_3_out_17));
  _4_bit_Multiplier u_4_bit_multiplier_1 (
    .Left(n8_bit_condition_3_out_10), .Right(n8_bit_condition_4_out_10), .out_4(n4_bit_multiplier_1_out_4),
    .Zero(n4_bit_multiplier_1_zero));
  _8_bit_or_Gate u_8_bit_or_gate_1 (
    .in_1(n4_bit_multiplier_1_out_4), .in_2(n8_bit_adder_subtractor_1_result), ._0(n8_bit_or_gate_1__0),
    ._1(n8_bit_or_gate_1__1), ._2(n8_bit_or_gate_1__2), ._3(n8_bit_or_gate_1__3), ._4(n8_bit_or_gate_1__4),
    ._5(n8_bit_or_gate_1__5), ._6(n8_bit_or_gate_1__6), ._7(n8_bit_or_gate_1__7));
  Register A_out (
    .Clock(Clock), .R_W(R_W), ._7(n8_bit_or_gate_1__7), ._6(n8_bit_or_gate_1__6), ._5(n8_bit_or_gate_1__5),
    ._4(n8_bit_or_gate_1__4), ._3(n8_bit_or_gate_1__3), ._2(n8_bit_or_gate_1__2), ._1(n8_bit_or_gate_1__1),
    ._0(n8_bit_or_gate_1__0), ._7_2(A_out_Output[7]), ._6_2(A_out_Output[6]), ._5_2(A_out_Output[5]),
    ._4_2(A_out_Output[4]), ._3_2(A_out_Output[3]), ._2_2(A_out_Output[2]), ._1_2(A_out_Output[1]),
    ._0_2(A_out_Output[0]));
  Register Right (
    .Clock(Clock), .R_W(R_W), ._7(Right_Input[7]), ._6(Right_Input[6]), ._5(Right_Input[5]),
    ._4(Right_Input[4]), ._3(Right_Input[3]), ._2(Right_Input[2]), ._1(Right_Input[1]), ._0(Right_Input[0]),
    ._7_2(Right__7_2), ._6_2(Right__6_2), ._5_2(Right__5_2), ._4_2(Right__4_2), ._3_2(Right__3_2),
    ._2_2(Right__2_2), ._1_2(Right__1_2), ._0_2(Right__0_2));
  _8_bit_Condition_Gate u_8_bit_condition_4 (
    .Condition(in_4[1]), .in_2(Right__0_2), .in_3(Right__1_2), .in_4(Right__2_2), .in_5(Right__3_2),
    .in_6(Right__4_2), .in_7(Right__5_2), .in_8(Right__6_2), .in_9(Right__7_2),
    .out_10(n8_bit_condition_4_out_10[0]), .out_11(n8_bit_condition_4_out_10[1]),
    .out_12(n8_bit_condition_4_out_10[2]), .out_13(n8_bit_condition_4_out_10[3]),
    .out_14(n8_bit_condition_4_out_14), .out_15(n8_bit_condition_4_out_15),
    .out_16(n8_bit_condition_4_out_16), .out_17(n8_bit_condition_4_out_17));
  and and_3 (and_3_out, n4_bit_multiplier_1_zero, in_4[1]);
  or or_1 (or_1_out, and_2_out, and_3_out);
  Status_Register Status (
    .Overflow(n8_bit_adder_subtractor_1_overflow), .Zero(or_1_out), .Overflow_2(Overflow), .Zero_2(Zero),
    .Clock(Clock));  // open: _3, _2, _3_2, _2_2
endmodule

module Register (
  input  _7,
  input  _6,
  input  _5,
  input  _4,
  input  _3,
  input  _2,
  input  _1,
  input  _0,
  input  Clock,
  input  R_W,
  output _7_2,
  output _6_2,
  output _5_2,
  output _4_2,
  output _3_2,
  output _2_2,
  output _1_2,
  output _0_2
);

  D_Flip_Flop d_ff_1 (.clk(Clock), .D(_7), .Q(_7_2), .en(R_W));  // open: Qn, preset, reset
  D_Flip_Flop d_ff_2 (.clk(Clock), .D(_6), .Q(_6_2), .en(R_W));  // open: Qn, preset, reset
  D_Flip_Flop d_ff_3 (.clk(Clock), .D(_5), .Q(_5_2), .en(R_W));  // open: Qn, preset, reset
  D_Flip_Flop d_ff_4 (.clk(Clock), .D(_4), .Q(_4_2), .en(R_W));  // open: Qn, preset, reset
  D_Flip_Flop d_ff_5 (.clk(Clock), .D(_3), .Q(_3_2), .en(R_W));  // open: Qn, preset, reset
  D_Flip_Flop d_ff_6 (.clk(Clock), .D(_2), .Q(_2_2), .en(R_W));  // open: Qn, preset, reset
  D_Flip_Flop d_ff_7 (.clk(Clock), .D(_1), .Q(_1_2), .en(R_W));  // open: Qn, preset, reset
  D_Flip_Flop d_ff_8 (.clk(Clock), .D(_0), .Q(_0_2), .en(R_W));  // open: Qn, preset, reset
endmodule

// A/S
module _8_bit_Adder_Subtractor (
  input  [7:0] Left_Input,
  input  [7:0] Right_Input,
  input  Add_Subtract,
  output Overflow,
  output Zero,
  output [7:0] Result
);

  wire _0_carry_out, _1_carry_out, _2_carry_out, _3_carry_out, _4_carry_out, _5_carry_out, _6_carry_out,
       multiplexer_1_out, multiplexer_2_out, multiplexer_3_out, multiplexer_4_out, multiplexer_5_out,
       multiplexer_6_out, multiplexer_7_out, multiplexer_8_out, not_1_out, not_2_out, not_3_out, not_4_out,
       not_5_out, not_6_out, not_7_out, not_8_out, not_9_out, not_10_out, not_11_out, not_12_out, not_13_out,
       not_14_out, not_15_out, not_16_out;

  not not_1 (not_1_out, Left_Input[7]);
  Multiplexer #(.enable("false")) multiplexer_1 (
    .in0(Left_Input[7]), .in1(not_1_out), .out(multiplexer_1_out), .sel(Add_Subtract));
  _1_bit_Full_Adder _7 (
    .A(Right_Input[7]), .B(multiplexer_1_out), .Carry_in(_6_carry_out), .Sum(Result[7]), .Carry_out(Overflow));
  not not_2 (not_2_out, Left_Input[6]);
  Multiplexer #(.enable("false")) multiplexer_2 (
    .in0(Left_Input[6]), .in1(not_2_out), .out(multiplexer_2_out), .sel(Add_Subtract));
  _1_bit_Full_Adder _6 (
    .A(Right_Input[6]), .B(multiplexer_2_out), .Carry_in(_5_carry_out), .Sum(Result[6]),
    .Carry_out(_6_carry_out));
  not not_3 (not_3_out, Left_Input[5]);
  Multiplexer #(.enable("false")) multiplexer_3 (
    .in0(Left_Input[5]), .in1(not_3_out), .out(multiplexer_3_out), .sel(Add_Subtract));
  _1_bit_Full_Adder _5 (
    .A(Right_Input[5]), .B(multiplexer_3_out), .Carry_in(_4_carry_out), .Sum(Result[5]),
    .Carry_out(_5_carry_out));
  not not_4 (not_4_out, Left_Input[4]);
  Multiplexer #(.enable("false")) multiplexer_4 (
    .in0(Left_Input[4]), .in1(not_4_out), .out(multiplexer_4_out), .sel(Add_Subtract));
  _1_bit_Full_Adder _4 (
    .A(Right_Input[4]), .B(multiplexer_4_out), .Carry_in(_3_carry_out), .Sum(Result[4]),
    .Carry_out(_4_carry_out));
  not not_5 (not_5_out, Left_Input[3]);
  Multiplexer #(.enable("false")) multiplexer_5 (
    .in0(Left_Input[3]), .in1(not_5_out), .out(multiplexer_5_out), .sel(Add_Subtract));
  _1_bit_Full_Adder _3 (
    .A(Right_Input[3]), .B(multiplexer_5_out), .Carry_in(_2_carry_out), .Sum(Result[3]),
    .Carry_out(_3_carry_out));
  not not_6 (not_6_out, Left_Input[2]);
  Multiplexer #(.enable("false")) multiplexer_6 (
    .in0(Left_Input[2]), .in1(not_6_out), .out(multiplexer_6_out), .sel(Add_Subtract));
  _1_bit_Full_Adder _2 (
    .A(Right_Input[2]), .B(multiplexer_6_out), .Carry_in(_1_carry_out), .Sum(Result[2]),
    .Carry_out(_2_carry_out));
  not not_7 (not_7_out, Left_Input[1]);
  Multiplexer #(.enable("false")) multiplexer_7 (
    .in0(Left_Input[1]), .in1(not_7_out), .out(multiplexer_7_out), .sel(Add_Subtract));
  _1_bit_Full_Adder _1 (
    .A(Right_Input[1]), .B(multiplexer_7_out), .Carry_in(_0_carry_out), .Sum(Result[1]),
    .Carry_out(_1_carry_out));
  not not_8 (not_8_out, Left_Input[0]);
  Multiplexer #(.enable("false")) multiplexer_8 (
    .in0(Left_Input[0]), .in1(not_8_out), .out(multiplexer_8_out), .sel(Add_Subtract));
  _1_bit_Full_Adder _0 (
    .A(Right_Input[0]), .B(multiplexer_8_out), .Carry_in(Add_Subtract), .Sum(Result[0]),
    .Carry_out(_0_carry_out));
  not not_9 (not_9_out, Result[0]);
  not not_10 (not_10_out, Result[1]);
  not not_11 (not_11_out, Result[2]);
  not not_12 (not_12_out, Result[3]);
  and and_1 (Zero, not_9_out, not_10_out, not_11_out, not_12_out, not_13_out, not_14_out, not_15_out, not_16_out);
  not not_13 (not_13_out, Result[4]);
  not not_14 (not_14_out, Result[5]);
  not not_15 (not_15_out, Result[6]);
  not not_16 (not_16_out, Result[7]);

  // Notes on the sheet:
  //   Add = 0, Subtract = 1
endmodule

// FA
module _1_bit_Full_Adder (
  input  A,
  input  B,
  input  Carry_in,
  output Sum,
  output Carry_out
);

  wire and_1_out, and_2_out, xor_1_out;

  xor xor_1 (xor_1_out, A, B);
  xor xor_2 (Sum, xor_1_out, Carry_in);
  and and_1 (and_1_out, Carry_in, xor_1_out);
  and and_2 (and_2_out, B, A);
  or or_1 (Carry_out, and_1_out, and_2_out);
endmodule

// M
module _4_bit_Multiplier (
  input  [3:0] Left,
  input  [3:0] Right,
  output Zero,
  output [7:0] out_4
);

  wire n1_bit_full_adder_2_carry_out, n1_bit_full_adder_2_sum, n1_bit_full_adder_3_carry_out,
       n1_bit_full_adder_4_carry_out, n1_bit_full_adder_5_carry_out, n1_bit_full_adder_5_sum,
       n1_bit_full_adder_6_carry_out, n1_bit_full_adder_6_sum, n1_bit_full_adder_7_carry_out,
       n1_bit_full_adder_8_carry_out, n1_bit_full_adder_8_sum, n1_bit_full_adder_9_carry_out,
       n1_bit_full_adder_9_sum, n1_bit_full_adder_10_carry_out, n1_bit_full_adder_10_sum,
       n1_bit_full_adder_11_carry_out, n1_bit_full_adder_12_carry_out, not_1_out, not_2_out, not_3_out,
       not_4_out, not_5_out, not_6_out, not_7_out, not_8_out, R0L1_out, R0L2_out, R0L3_out, R1L0_out,
       R1L1_out, R1L2_out, R1L3_out, R2L0_out, R2L1_out, R2L2_out, R2L3_out, R3L0_out, R3L1_out, R3L2_out,
       R3L3_out;

  and R3L3 (R3L3_out, Left[3], Right[3]);
  _1_bit_Full_Adder u_1_bit_full_adder_1 (
    .A(n1_bit_full_adder_2_carry_out), .B(R3L3_out), .Carry_in(n1_bit_full_adder_3_carry_out),
    .Sum(out_4[6]), .Carry_out(out_4[7]));
  and R3L2 (R3L2_out, Left[2], Right[3]);
  and R2L3 (R2L3_out, Left[3], Right[2]);
  _1_bit_Full_Adder u_1_bit_full_adder_2 (
    .A(R2L3_out), .B(R3L2_out), .Carry_in(n1_bit_full_adder_5_carry_out), .Sum(n1_bit_full_adder_2_sum),
    .Carry_out(n1_bit_full_adder_2_carry_out));
  _1_bit_Full_Adder u_1_bit_full_adder_3 (
    .A(n1_bit_full_adder_2_sum), .B(n1_bit_full_adder_6_carry_out), .Carry_in(n1_bit_full_adder_4_carry_out),
    .Sum(out_4[5]), .Carry_out(n1_bit_full_adder_3_carry_out));
  and R3L1 (R3L1_out, Left[1], Right[3]);
  and R2L2 (R2L2_out, Left[2], Right[2]);
  _1_bit_Full_Adder u_1_bit_full_adder_4 (
    .A(n1_bit_full_adder_7_carry_out), .B(n1_bit_full_adder_6_sum), .Carry_in(1'b0), .Sum(out_4[4]),
    .Carry_out(n1_bit_full_adder_4_carry_out));
  and R1L3 (R1L3_out, Left[3], Right[1]);
  _1_bit_Full_Adder u_1_bit_full_adder_5 (
    .A(R1L3_out), .B(R2L2_out), .Carry_in(n1_bit_full_adder_8_carry_out), .Sum(n1_bit_full_adder_5_sum),
    .Carry_out(n1_bit_full_adder_5_carry_out));
  _1_bit_Full_Adder u_1_bit_full_adder_6 (
    .A(n1_bit_full_adder_5_sum), .B(R3L1_out), .Carry_in(n1_bit_full_adder_9_carry_out),
    .Sum(n1_bit_full_adder_6_sum), .Carry_out(n1_bit_full_adder_6_carry_out));
  and R3L0 (R3L0_out, Left[0], Right[3]);
  and R2L1 (R2L1_out, Left[1], Right[2]);
  and R1L2 (R1L2_out, Left[2], Right[1]);
  _1_bit_Full_Adder u_1_bit_full_adder_7 (
    .A(n1_bit_full_adder_9_sum), .B(R3L0_out), .Carry_in(n1_bit_full_adder_11_carry_out), .Sum(out_4[3]),
    .Carry_out(n1_bit_full_adder_7_carry_out));
  and R0L3 (R0L3_out, Left[3], Right[0]);
  _1_bit_Full_Adder u_1_bit_full_adder_8 (
    .A(R0L3_out), .B(R1L2_out), .Carry_in(1'b0), .Sum(n1_bit_full_adder_8_sum),
    .Carry_out(n1_bit_full_adder_8_carry_out));
  _1_bit_Full_Adder u_1_bit_full_adder_9 (
    .A(n1_bit_full_adder_8_sum), .B(R2L1_out), .Carry_in(n1_bit_full_adder_10_carry_out),
    .Sum(n1_bit_full_adder_9_sum), .Carry_out(n1_bit_full_adder_9_carry_out));
  and R2L0 (R2L0_out, Left[0], Right[2]);
  not not_1 (not_1_out, out_4[0]);
  not not_2 (not_2_out, out_4[1]);
  not not_3 (not_3_out, out_4[2]);
  not not_4 (not_4_out, out_4[3]);
  not not_5 (not_5_out, out_4[4]);
  not not_6 (not_6_out, out_4[5]);
  not not_7 (not_7_out, out_4[6]);
  not not_8 (not_8_out, out_4[7]);
  and R1L1 (R1L1_out, Left[1], Right[1]);
  and R0L2 (R0L2_out, Left[2], Right[0]);
  _1_bit_Full_Adder u_1_bit_full_adder_10 (
    .A(R0L2_out), .B(R1L1_out), .Carry_in(1'b0), .Sum(n1_bit_full_adder_10_sum),
    .Carry_out(n1_bit_full_adder_10_carry_out));
  _1_bit_Full_Adder u_1_bit_full_adder_11 (
    .A(n1_bit_full_adder_10_sum), .B(R2L0_out), .Carry_in(n1_bit_full_adder_12_carry_out), .Sum(out_4[2]),
    .Carry_out(n1_bit_full_adder_11_carry_out));
  and and_1 (Zero, not_1_out, not_2_out, not_3_out, not_4_out, not_5_out, not_6_out, not_7_out, not_8_out);
  and R0L1 (R0L1_out, Left[1], Right[0]);
  and R1L0 (R1L0_out, Left[0], Right[1]);
  _1_bit_Full_Adder u_1_bit_full_adder_12 (
    .A(R1L0_out), .B(R0L1_out), .Carry_in(1'b0), .Sum(out_4[1]), .Carry_out(n1_bit_full_adder_12_carry_out));
  and R0L0 (out_4[0], Left[0], Right[0]);
endmodule

module _8_bit_Condition_Gate (
  input  Condition,
  input  in_2,
  input  in_3,
  input  in_4,
  input  in_5,
  input  in_6,
  input  in_7,
  input  in_8,
  input  in_9,
  output out_10,
  output out_11,
  output out_12,
  output out_13,
  output out_14,
  output out_15,
  output out_16,
  output out_17
);

  and _0 (out_10, in_2, Condition);
  and _1 (out_11, in_3, Condition);
  and _2 (out_12, in_4, Condition);
  and _3 (out_13, in_5, Condition);
  and _4 (out_14, in_6, Condition);
  and _5 (out_15, in_7, Condition);
  and _6 (out_16, in_8, Condition);
  and _7 (out_17, in_9, Condition);
endmodule

module Status_Register (
  input  _3,
  input  _2,
  input  Overflow,
  input  Zero,
  input  Clock,
  output _3_2,
  output _2_2,
  output Overflow_2,
  output Zero_2
);

  D_Flip_Flop d_ff_1 (.clk(Clock), .D(_3), .Q(_3_2));  // open: Qn, preset, en, reset
  D_Flip_Flop d_ff_2 (.clk(Clock), .D(_2), .Q(_2_2));  // open: Qn, preset, en, reset
  D_Flip_Flop d_ff_3 (.clk(Clock), .D(Overflow), .Q(Overflow_2));  // open: Qn, preset, en, reset
  D_Flip_Flop d_ff_4 (.clk(Clock), .D(Zero), .Q(Zero_2));  // open: Qn, preset, en, reset
endmodule

module _8_bit_or_Gate (
  input  [7:0] in_1,
  input  [7:0] in_2,
  output _0,
  output _1,
  output _2,
  output _3,
  output _4,
  output _5,
  output _6,
  output _7
);

  or or_1 (_0, in_1[0], in_2[0]);
  or or_2 (_1, in_1[1], in_2[1]);
  or or_3 (_2, in_1[2], in_2[2]);
  or or_4 (_3, in_1[3], in_2[3]);
  or or_5 (_4, in_1[4], in_2[4]);
  or or_6 (_5, in_1[5], in_2[5]);
  or or_7 (_6, in_1[6], in_2[6]);
  or or_8 (_7, in_1[7], in_2[7]);
endmodule
