// Logisim project CPU.circ as structural Verilog: 4 circuits, main circuit main
module main (
  input  [7:0] Input,
  input  in_2,
  output [7:0] Display
);

  wire and_1_out, and_2_out, and_3_out, and_4_out, bz_bnz_1_out_6, demultiplexer_2_out0,
       demultiplexer_2_out1, demultiplexer_3_out0, demultiplexer_3_out1, j_k_ff_1_q, j_k_ff_2_q, ld_1_out_6,
       main_1_alu, main_1_alu_op_rx, main_1_alu_op_ry, main_1_bnz, main_1_bz, main_1_inp, main_1_ld,
       main_1_out_14, main_1_prt, main_1_rn, main_1_str, multiplexer_1_out, multiplexer_2_out,
       multiplexer_3_out, not_1_out, not_2_out, not_3_out, not_4_out, not_5_out, or_2_out, or_4_out,
       or_5_out, pc_delay_1_out_2, str_1_out_6;
  wire [1:0] main_1_op_code;
  wire [3:0] main_1_out_13, PC_Increment_out_5;
  wire [7:0] ALU_a_out_output, Data_Cache_out_5, demultiplexer_1_out0, demultiplexer_1_out1,
       demultiplexer_4_out0, demultiplexer_4_out1, Instruction_Cache_out_5, Instruction_Register_out_4,
       ld_1_r0, ld_1_r1, multiplexer_4_out, multiplexer_5_out, multiplexer_6_out, n8_bit_condition_1_out_10,
       n8_bit_condition_2_out_17, or_1_out, or_3_out, R0_out_4, R1_out_4, str_1_out_5;

  PC_Delay pc_delay_1 (.out_2(pc_delay_1_out_2), .in_1(and_1_out));
  not not_1 (not_1_out, pc_delay_1_out_2);
  REGISTER_main Instruction_Register (
    .R_W(pc_delay_1_out_2), .out_4(Instruction_Register_out_4), .INPUT(Instruction_Cache_out_5),
    .CLOCK(and_1_out));
  PC_Increment PC_Increment (
    .in_1(and_1_out), .out_5(PC_Increment_out_5), .in_3(bz_bnz_1_out_6), .in_4(main_1_out_13), .R_W(not_1_out));
  CU_main main_1 (
    .in_1(Instruction_Register_out_4), .ALU(main_1_alu), .OP_CODE(main_1_op_code),
    .ALU_OP_Rx(main_1_alu_op_rx), .ALU_OP_Ry(main_1_alu_op_ry), .STR(main_1_str), .LD(main_1_ld),
    .BZ(main_1_bz), .BNZ(main_1_bnz), .PRT(main_1_prt), .INP(main_1_inp), .Rn(main_1_rn),
    .out_13(main_1_out_13), .out_14(main_1_out_14));
  _8_bit_Condition_Gate u_8_bit_condition_1 (
    .in_2(Input[0]), .in_3(Input[1]), .in_4(Input[2]), .in_5(Input[3]), .in_6(Input[4]), .in_7(Input[5]),
    .in_8(Input[6]), .in_9(Input[7]), .out_10(n8_bit_condition_1_out_10[0]),
    .out_11(n8_bit_condition_1_out_10[1]), .out_12(n8_bit_condition_1_out_10[2]),
    .out_13(n8_bit_condition_1_out_10[3]), .out_14(n8_bit_condition_1_out_10[4]),
    .out_15(n8_bit_condition_1_out_10[5]), .out_16(n8_bit_condition_1_out_10[6]),
    .out_17(n8_bit_condition_1_out_10[7]), .Condition(main_1_inp));
  Demultiplexer #(.width(8), .enable("false")) demultiplexer_1 (
    .out0(demultiplexer_1_out0), .out1(demultiplexer_1_out1), .in(n8_bit_condition_1_out_10), .sel(main_1_rn));
  InstructionCache_main Instruction_Cache (
    .Clock(and_1_out), .R_W(1'b0), .Address(PC_Increment_out_5), .out_5(Instruction_Cache_out_5));  // open: Input
  not not_2 (not_2_out, main_1_out_14);
  and and_1 (and_1_out, in_2, not_2_out);
  and and_2 (and_2_out, and_1_out, main_1_alu);
  and and_3 (and_3_out, 1'b1, main_1_alu);
  BZ_BNZ bz_bnz_1 (
    .Rn(main_1_rn), .BZ(main_1_bz), .BNZ(main_1_bnz), .R0(R0_out_4), .R1(R1_out_4), .out_6(bz_bnz_1_out_6));
  STR str_1 (.Rn(main_1_rn), .STR(main_1_str), .R0(R0_out_4), .R1(R1_out_4), .out_6(str_1_out_6), .out_5(str_1_out_5));
  LD ld_1 (.Rn(main_1_rn), .LD(main_1_ld), .out_6(ld_1_out_6), .in_1(Data_Cache_out_5), .R0(ld_1_r0), .R1(ld_1_r1));
  Multiplexer #(.enable("false")) multiplexer_1 (
    .in0(and_1_out), .in1(j_k_ff_1_q), .out(multiplexer_1_out), .sel(main_1_alu));
  not not_3 (not_3_out, ld_1_out_6);
  J_K_Flip_Flop j_k_ff_1 (.J(and_3_out), .clk(and_2_out), .K(1'b1), .Q(j_k_ff_1_q));  // open: Qn, preset, en, reset
  not not_4 (not_4_out, j_k_ff_2_q);
  J_K_Flip_Flop j_k_ff_2 (
    .J(and_3_out), .clk(multiplexer_1_out), .K(1'b1), .Q(j_k_ff_2_q));  // open: Qn, preset, en, reset
  Demultiplexer #(.enable("false")) demultiplexer_2 (
    .out0(demultiplexer_2_out0), .out1(demultiplexer_2_out1), .in(not_3_out), .sel(main_1_rn));
  Demultiplexer #(.enable("false")) demultiplexer_3 (
    .out0(demultiplexer_3_out0), .out1(demultiplexer_3_out1), .in(not_4_out), .sel(main_1_alu_op_rx));
  assign or_1_out = ld_1_r0 | demultiplexer_4_out0 | demultiplexer_1_out0;  // OR_Gate or_1, 8 bits wide
  or or_2 (or_2_out, demultiplexer_2_out0, main_1_inp);
  assign or_3_out = demultiplexer_1_out1 | demultiplexer_4_out1 | ld_1_r1;  // OR_Gate or_3, 8 bits wide
  or or_4 (or_4_out, demultiplexer_2_out1, main_1_inp);
  and and_4 (and_4_out, str_1_out_6, ld_1_out_6);
  Multiplexer #(.enable("false")) multiplexer_2 (
    .in0(or_2_out), .in1(demultiplexer_3_out0), .out(multiplexer_2_out), .sel(main_1_alu));
  Multiplexer #(.enable("false")) multiplexer_3 (
    .in0(or_4_out), .in1(demultiplexer_3_out1), .out(multiplexer_3_out), .sel(main_1_alu));
  REGISTER_main R0 (.R_W(multiplexer_2_out), .out_4(R0_out_4), .INPUT(or_1_out), .CLOCK(and_1_out));
  REGISTER_main R1 (.R_W(multiplexer_3_out), .out_4(R1_out_4), .INPUT(or_3_out), .CLOCK(and_1_out));
  or or_5 (or_5_out, multiplexer_2_out, multiplexer_3_out);
  DataCache_main Data_Cache (
    .Clock(and_1_out), .Input(str_1_out_5), .R_W(and_4_out), .Address(main_1_out_13), .out_5(Data_Cache_out_5));
  Demultiplexer #(.width(8), .enable("false")) demultiplexer_4 (
    .out0(demultiplexer_4_out0), .out1(demultiplexer_4_out1), .in(n8_bit_condition_2_out_17),
    .sel(main_1_alu_op_rx));
  _8_bit_Condition_Gate u_8_bit_condition_2 (
    .in_2(ALU_a_out_output[7]), .in_3(ALU_a_out_output[6]), .in_4(ALU_a_out_output[5]),
    .in_5(ALU_a_out_output[4]), .in_6(ALU_a_out_output[3]), .in_7(ALU_a_out_output[2]),
    .in_8(ALU_a_out_output[1]), .in_9(ALU_a_out_output[0]), .out_10(n8_bit_condition_2_out_17[7]),
    .out_11(n8_bit_condition_2_out_17[6]), .out_12(n8_bit_condition_2_out_17[5]),
    .out_13(n8_bit_condition_2_out_17[4]), .out_14(n8_bit_condition_2_out_17[3]),
    .out_15(n8_bit_condition_2_out_17[2]), .out_16(n8_bit_condition_2_out_17[1]),
    .out_17(n8_bit_condition_2_out_17[0]), .Condition(main_1_alu));
  Multiplexer #(.width(8), .enable("false")) multiplexer_4 (
    .in0(R0_out_4), .in1(R1_out_4), .out(multiplexer_4_out), .sel(main_1_rn));
  Multiplexer #(.width(8), .enable("false")) multiplexer_5 (
    .in0(R0_out_4), .in1(R1_out_4), .out(multiplexer_5_out), .sel(main_1_alu_op_rx));
  ALU_main ALU (
    .Left_Input(multiplexer_5_out), .Right_Input(multiplexer_6_out), .in_4(main_1_op_code),
    .Clock(and_1_out), .A_out_Output(ALU_a_out_output), .R_W(not_5_out));  // open: Overflow, Zero
  not not_5 (not_5_out, or_5_out);
  Multiplexer #(.width(8), .enable("false")) multiplexer_6 (
    .in0(R0_out_4), .in1(R1_out_4), .out(multiplexer_6_out), .sel(main_1_alu_op_ry));
  _8_bit_Condition_Gate u_8_bit_condition_3 (
    .in_2(multiplexer_4_out[0]), .in_3(multiplexer_4_out[1]), .in_4(multiplexer_4_out[2]),
    .in_5(multiplexer_4_out[3]), .in_6(multiplexer_4_out[4]), .in_7(multiplexer_4_out[5]),
    .in_8(multiplexer_4_out[6]), .in_9(multiplexer_4_out[7]), .out_10(Display[0]), .out_11(Display[1]),
    .out_12(Display[2]), .out_13(Display[3]), .out_14(Display[4]), .out_15(Display[5]), .out_16(Display[6]),
    .out_17(Display[7]), .Condition(main_1_prt));
endmodule

module LD (
  input  [7:0] in_1,
  input  Rn,
  input  LD,
  output [7:0] R0,
  output [7:0] R1,
  output out_6
);

  wire [7:0] n8_bit_condition_1_out_10;

  not not_1 (out_6, LD);
  _8_bit_Condition_Gate u_8_bit_condition_1 (
    .in_2(in_1[0]), .in_3(in_1[1]), .in_4(in_1[2]), .in_5(in_1[3]), .in_6(in_1[4]), .in_7(in_1[5]),
    .in_8(in_1[6]), .in_9(in_1[7]), .out_10(n8_bit_condition_1_out_10[0]),
    .out_11(n8_bit_condition_1_out_10[1]), .out_12(n8_bit_condition_1_out_10[2]),
    .out_13(n8_bit_condition_1_out_10[3]), .out_14(n8_bit_condition_1_out_10[4]),
    .out_15(n8_bit_condition_1_out_10[5]), .out_16(n8_bit_condition_1_out_10[6]),
    .out_17(n8_bit_condition_1_out_10[7]), .Condition(LD));
  Demultiplexer #(.width(8), .enable("false")) demultiplexer_1 (
    .out0(R0), .out1(R1), .in(n8_bit_condition_1_out_10), .sel(Rn));
endmodule

module STR (
  input  [7:0] R0,
  input  [7:0] R1,
  input  Rn,
  input  STR,
  output [7:0] out_5,
  output out_6
);

  Multiplexer #(.width(8), .enable("false")) multiplexer_1 (.in0(R0), .in1(R1), .out(out_5), .sel(Rn));

  assign out_6 = STR;
endmodule

module PC_Delay (
  input  in_1,
  output out_2
);

  wire j_k_ff_1_q, j_k_ff_2_q;

  J_K_Flip_Flop j_k_ff_1 (.J(1'b1), .clk(in_1), .K(1'b1), .Q(j_k_ff_1_q));  // open: Qn, preset, en, reset
  J_K_Flip_Flop j_k_ff_2 (.J(1'b1), .clk(j_k_ff_1_q), .K(1'b1), .Q(j_k_ff_2_q));  // open: Qn, preset, en, reset
  J_K_Flip_Flop j_k_ff_3 (.J(1'b1), .clk(j_k_ff_2_q), .K(1'b1), .Q(out_2));  // open: Qn, preset, en, reset
endmodule
