// Logisim project CU.circ as structural Verilog: 1 circuit, main circuit main
module main (
  input  [7:0] in_1,
  output ALU,
  output [1:0] OP_CODE,
  output ALU_OP_Rx,
  output ALU_OP_Ry,
  output STR,
  output LD,
  output BZ,
  output BNZ,
  output PRT,
  output INP,
  output Rn,
  output [3:0] out_13,
  output out_14
);

  wire and_4_out, and_14_out, not_1_out, not_2_out, not_3_out, not_4_out, not_5_out, not_6_out, not_7_out,
       not_8_out, not_9_out, not_10_out, not_11_out, not_12_out, not_13_out, not_14_out, not_15_out,
       not_16_out, not_17_out, not_18_out, not_19_out, not_20_out, not_21_out, not_22_out, or_1_out;

  not not_1 (not_1_out, in_1[7]);
  not not_2 (not_2_out, in_1[6]);
  not not_3 (not_3_out, in_1[5]);
  not not_4 (not_4_out, in_1[4]);
  not not_5 (not_5_out, in_1[2]);
  not not_6 (not_6_out, in_1[7]);
  not not_7 (not_7_out, in_1[6]);
  not not_8 (not_8_out, in_1[5]);
  not not_9 (not_9_out, in_1[4]);
  not not_10 (not_10_out, in_1[7]);
  not not_11 (not_11_out, in_1[6]);
  not not_12 (not_12_out, in_1[5]);
  not not_13 (not_13_out, in_1[4]);
  not not_14 (not_14_out, in_1[3]);
  not not_15 (not_15_out, in_1[2]);
  and and_1 (PRT, not_1_out, not_2_out, not_3_out, not_4_out, in_1[3], not_5_out);
  and and_2 (INP, not_6_out, not_7_out, not_8_out, not_9_out, in_1[3], in_1[2]);
  and and_3 (out_14, not_10_out, not_11_out, not_12_out, not_13_out, not_15_out, in_1[1], in_1[0]);
  and and_4 (and_4_out, in_1[1], or_1_out);
  or or_1 (or_1_out, PRT, INP);
  not not_16 (not_16_out, in_1[6]);
  not not_17 (not_17_out, in_1[5]);
  not not_18 (not_18_out, in_1[6]);
  not not_19 (not_19_out, in_1[5]);
  and and_5 (STR, in_1[7], not_16_out, not_17_out);
  and and_6 (LD, in_1[7], not_18_out, in_1[5]);
  and and_7 (BZ, in_1[7], in_1[6], not_19_out);
  and and_8 (BNZ, in_1[7], in_1[6], in_1[5]);
  not not_20 (not_20_out, in_1[7]);
  not not_21 (not_21_out, in_1[6]);
  not not_22 (not_22_out, in_1[5]);
  and and_9 (out_13[3], in_1[3], in_1[7]);
  and and_10 (out_13[2], in_1[2], in_1[7]);
  and and_11 (out_13[1], in_1[1], in_1[7]);
  and and_12 (out_13[0], in_1[0], in_1[7]);
  and and_13 (ALU, not_20_out, not_22_out, in_1[4]);
  and and_14 (and_14_out, in_1[7], in_1[4]);
  and and_15 (ALU_OP_Rx, in_1[1], ALU);
  and and_16 (ALU_OP_Ry, in_1[0], ALU);
  or or_2 (Rn, and_14_out, and_4_out);
  and and_17 (OP_CODE[1], in_1[3], ALU);
  and and_18 (OP_CODE[0], in_1[2], ALU);

  // Notes on the sheet:
  //   in_1: pull=up
  //   prt
  //   inp
  //   DATA
  //   io
  //   IO
  //   ADDRESOP
  //   addrop
  //   DATA
  //   addressop
  //   addressop
  //   DATA
  //   io
  //   RETURN
  //   ADDRESS
endmodule
