// Logisim project DISPLAY.circ as structural Verilog: 2 circuits, main circuit main
module main (
  input  [7:0] Input_To_Display
);

  wire display_calculator_1_a, display_calculator_1_b, display_calculator_1_c, display_calculator_1_d,
       display_calculator_1_e, display_calculator_1_f, display_calculator_1_g;

  Display_Calculator display_calculator_1 (
    .a(display_calculator_1_a), .b(display_calculator_1_b), .c(display_calculator_1_c),
    .d(display_calculator_1_d), .e(display_calculator_1_e), .f(display_calculator_1_f),
    .g(display_calculator_1_g), ._8_bit_Input(Input_To_Display));
  _7_Segment_Display u_7_segment_display_1 (
    .g(display_calculator_1_g), .f(display_calculator_1_f), .a(display_calculator_1_a),
    .b(display_calculator_1_b), .e(display_calculator_1_e), .d(display_calculator_1_d),
    .c(display_calculator_1_c));  // open: dp

  // Notes on the sheet:
  //   a
endmodule

module Display_Calculator (
  input  [7:0] _8_bit_Input,
  output a,
  output b,
  output c,
  output d,
  output e,
  output f,
  output g
);

  wire and_1_out, and_2_out, and_3_out, and_4_out, and_5_out, and_6_out, and_7_out, and_8_out, and_9_out,
       and_10_out, and_11_out, and_12_out, and_13_out, and_14_out, and_15_out, and_16_out, and_17_out,
       and_18_out, and_19_out, and_20_out, and_21_out, and_24_out, and_25_out, not_1_out, not_2_out,
       not_3_out, not_4_out, not_5_out, not_6_out, not_7_out, not_8_out, not_9_out, not_10_out, not_11_out,
       not_12_out, not_13_out, not_14_out, not_15_out, not_16_out, not_17_out, not_18_out, not_19_out,
       not_20_out, not_21_out, not_22_out, not_23_out, or_2_out, or_3_out, or_4_out, or_5_out, or_6_out,
       or_7_out, or_8_out;

  not not_1 (not_1_out, _8_bit_Input[2]);
  and and_1 (and_1_out, _8_bit_Input[2], _8_bit_Input[0]);
  not not_2 (not_2_out, _8_bit_Input[0]);
  not not_3 (not_3_out, _8_bit_Input[2]);
  not not_4 (not_4_out, _8_bit_Input[0]);
  not not_5 (not_5_out, _8_bit_Input[0]);
  not not_6 (not_6_out, _8_bit_Input[2]);
  not not_7 (not_7_out, _8_bit_Input[0]);
  not not_8 (not_8_out, _8_bit_Input[3]);
  not not_9 (not_9_out, _8_bit_Input[2]);
  not not_10 (not_10_out, _8_bit_Input[1]);
  and and_2 (and_2_out, not_3_out, _8_bit_Input[1]);
  and and_3 (and_3_out, not_3_out, not_4_out);
  and and_4 (and_4_out, _8_bit_Input[3], _8_bit_Input[1]);
  and and_5 (and_5_out, _8_bit_Input[2], not_7_out);
  not not_11 (not_11_out, _8_bit_Input[1]);
  or or_1 (a, _8_bit_Input[7], _8_bit_Input[6], _8_bit_Input[5], _8_bit_Input[4], or_2_out);
  or or_2 (or_2_out, _8_bit_Input[3], _8_bit_Input[1], and_1_out, and_6_out);
  and and_6 (and_6_out, not_1_out, not_2_out);
  and and_7 (and_7_out, not_8_out, not_9_out);
  and and_8 (and_8_out, not_9_out, not_10_out);
  and and_9 (and_9_out, _8_bit_Input[1], not_4_out);
  and and_10 (and_10_out, _8_bit_Input[3], _8_bit_Input[2]);
  and and_11 (and_11_out, _8_bit_Input[2], not_11_out);
  not not_12 (not_12_out, _8_bit_Input[2]);
  not not_13 (not_13_out, _8_bit_Input[1]);
  not not_14 (not_14_out, _8_bit_Input[0]);
  not not_15 (not_15_out, _8_bit_Input[7]);
  not not_16 (not_16_out, _8_bit_Input[6]);
  not not_17 (not_17_out, _8_bit_Input[5]);
  not not_18 (not_18_out, _8_bit_Input[4]);
  and and_12 (and_12_out, not_8_out, _8_bit_Input[1], _8_bit_Input[0]);
  and and_13 (and_13_out, not_8_out, not_10_out, not_19_out);
  not not_19 (not_19_out, _8_bit_Input[0]);
  and and_14 (and_14_out, _8_bit_Input[2], _8_bit_Input[0], not_20_out);
  not not_20 (not_20_out, _8_bit_Input[1]);
  and and_15 (and_15_out, _8_bit_Input[1], not_5_out);
  and and_16 (and_16_out, not_5_out, not_6_out);
  and and_17 (and_17_out, not_11_out, not_7_out);
  and and_18 (and_18_out, not_12_out, _8_bit_Input[1]);
  and and_19 (and_19_out, _8_bit_Input[2], not_14_out);
  or or_3 (or_3_out, and_21_out, and_24_out, and_25_out);
  and and_20 (and_20_out, not_13_out, _8_bit_Input[2]);
  or or_4 (or_4_out, and_7_out, and_12_out, and_8_out, and_13_out);
  or or_5 (or_5_out, and_10_out, and_4_out, and_15_out, and_16_out);
  or or_6 (or_6_out, _8_bit_Input[3], and_5_out, and_11_out, and_17_out);
  and and_21 (and_21_out, not_21_out, _8_bit_Input[2]);
  not not_21 (not_21_out, _8_bit_Input[3]);
  not not_22 (not_22_out, _8_bit_Input[2]);
  not not_23 (not_23_out, _8_bit_Input[1]);
  or or_7 (or_7_out, _8_bit_Input[3], and_2_out, and_3_out, and_14_out, and_9_out);
  or or_8 (or_8_out, _8_bit_Input[3], and_18_out, and_20_out, and_19_out);
  and and_22 (b, not_15_out, not_16_out, not_17_out, not_18_out, or_4_out);
  and and_23 (c, not_15_out, not_16_out, not_17_out, not_18_out, or_3_out);
  and and_24 (and_24_out, not_21_out, _8_bit_Input[0]);
  and and_25 (and_25_out, not_22_out, not_23_out);
  or or_9 (e, _8_bit_Input[7], _8_bit_Input[6], _8_bit_Input[5], _8_bit_Input[4], or_5_out);
  or or_10 (g, _8_bit_Input[7], _8_bit_Input[6], _8_bit_Input[5], _8_bit_Input[4], or_8_out);
  or or_11 (d, _8_bit_Input[7], _8_bit_Input[6], _8_bit_Input[5], _8_bit_Input[4], or_7_out);
  or or_12 (f, _8_bit_Input[7], _8_bit_Input[6], _8_bit_Input[5], _8_bit_Input[4], or_6_out);
endmodule
