// Logisim project EXTRACIRCUIT.circ as structural Verilog
module PC_Increment (
  input  in_1,
  input  R_W,
  input  in_3,
  input  [3:0] in_4,
  output [3:0] out_5
);

  wire j_k_ff_1_q, not_1_out;
  wire [3:0] main_2_a_out_output, multiplexer_1_out;
  wire [7:4] main_2_a_out_output_2, undriven;

  Multiplexer #(.width(4), .enable("false")) multiplexer_1 (
    .in0(main_2_a_out_output), .in1(in_4), .out(multiplexer_1_out), .sel(in_3));
  PC_main main_1 (.in_3(R_W), .out_4(out_5), .in_1(multiplexer_1_out), .in_2(in_1));
  not not_1 (not_1_out, R_W);
  ALU_main main_2 (
    .Left_Input({undriven, out_5}), .Right_Input(8'h1), .in_4(2'b00), .Clock(j_k_ff_1_q),
    .A_out_Output({main_2_a_out_output_2, main_2_a_out_output}), .R_W(not_1_out));  // open: Overflow, Zero
  J_K_Flip_Flop j_k_ff_1 (.J(1'b1), .clk(in_1), .K(1'b1), .Q(j_k_ff_1_q));  // open: Qn, preset, en, reset
endmodule

module BZ_BNZ (
  input  BZ,
  input  BNZ,
  input  Rn,
  input  [7:0] R0,
  input  [7:0] R1,
  output out_6
);

  wire and_1_out, and_2_out, not_1_out, or_2_out;
  wire [7:0] multiplexer_1_out;

  or or_1 (out_6, and_1_out, and_2_out);
  and and_1 (and_1_out, BZ, not_1_out);
  not not_1 (not_1_out, or_2_out);
  or or_2 (or_2_out, multiplexer_1_out[7], multiplexer_1_out[6], multiplexer_1_out[5], multiplexer_1_out[4], multiplexer_1_out[3], multiplexer_1_out[2], multiplexer_1_out[1], multiplexer_1_out[0]);
  and and_2 (and_2_out, BNZ, or_2_out);
  Multiplexer #(.width(8), .enable("false")) multiplexer_1 (.in0(R0), .in1(R1), .out(multiplexer_1_out), .sel(Rn));
endmodule
