// Logisim project Everything.circ as structural Verilog: 1 circuit, main circuit main
module main (
  input  _0_Off_On,
  input  _1,
  input  _2,
  input  _3,
  input  _4,
  input  _5,
  input  _6,
  input  _7,
  input  _8,
  input  _9
);

  wire and_1_out, clock_1_out, display_calculator_1_a, display_calculator_1_b, display_calculator_1_c,
       display_calculator_1_d, display_calculator_1_e, display_calculator_1_f, display_calculator_1_g,
       not_1_out;
  wire [7:0] INPUT_out_13, main_1_display;

  Clock clock_1 (.out(clock_1_out));
  and and_1 (and_1_out, clock_1_out, not_1_out);
  not not_1 (not_1_out, _0_Off_On);
  INPUT_main INPUT (
    .in_1(and_1_out), .in_2(_0_Off_On), .in_3(_1), .in_5(_2), .in_6(_3), .in_7(_4), .in_8(_5), .in_9(_6),
    .in_10(_7), .in_11(_8), .in_12(_9), .in_4(and_1_out), .out_13(INPUT_out_13));
  CPU_main main_1 (.Input(INPUT_out_13), .in_2(and_1_out), .Display(main_1_display));
  Display_Calculator display_calculator_1 (
    .a(display_calculator_1_a), .b(display_calculator_1_b), .c(display_calculator_1_c),
    .d(display_calculator_1_d), .e(display_calculator_1_e), .f(display_calculator_1_f),
    .g(display_calculator_1_g), ._8_bit_Input(main_1_display));
  _7_Segment_Display u_7_segment_display_1 (
    .g(display_calculator_1_g), .f(display_calculator_1_f), .a(display_calculator_1_a),
    .b(display_calculator_1_b), .e(display_calculator_1_e), .d(display_calculator_1_d),
    .c(display_calculator_1_c));  // open: dp
endmodule
