// Logisim project INPUT.circ as structural Verilog: 13 circuits, main circuit main
module main (
  input  in_1,
  input  in_2,
  input  in_3,
  input  in_4,
  input  in_5,
  input  in_6,
  input  in_7,
  input  in_8,
  input  in_9,
  input  in_10,
  input  in_11,
  input  in_12,
  output [7:0] out_13
);

  wire [7:0] merge_1_out_11, n0_1_out_2, n1_1_out_2, n2_1_out_2, n3_1_out_2, n4_1_out_2, n5_1_out_2,
       n6_1_out_2, n7_1_out_2, n8_1_out_2, n9_1_out_2;

  Button _0 ();  // open: out
  Button _1 ();  // open: out
  Button _2 ();  // open: out
  Button _3 ();  // open: out
  Button _4 ();  // open: out
  Button _5 ();  // open: out
  Button _6 ();  // open: out
  Button _7 ();  // open: out
  Button _8 ();  // open: out
  Button _9 ();  // open: out
  _0 u_0_1 (.in_1(in_2), .out_2(n0_1_out_2));
  _1 u_1_1 (.in_1(in_3), .out_2(n1_1_out_2));
  _2 u_2_1 (.in_1(in_5), .out_2(n2_1_out_2));
  _3 u_3_1 (.in_1(in_6), .out_2(n3_1_out_2));
  _4 u_4_1 (.in_1(in_7), .out_2(n4_1_out_2));
  _5 u_5_1 (.in_1(in_8), .out_2(n5_1_out_2));
  _6 u_6_1 (.in_1(in_9), .out_2(n6_1_out_2));
  _7 u_7_1 (.in_1(in_10), .out_2(n7_1_out_2));
  _8 u_8_1 (.in_1(in_11), .out_2(n8_1_out_2));
  _9 u_9_1 (.in_1(in_12), .out_2(n9_1_out_2));
  merge merge_1 (
    .in_1(n0_1_out_2), .in_2(n1_1_out_2), .in_3(n2_1_out_2), .in_4(n3_1_out_2), .in_5(n4_1_out_2),
    .in_6(n5_1_out_2), .in_7(n6_1_out_2), .in_8(n7_1_out_2), .in_9(n8_1_out_2), .in_10(n9_1_out_2),
    .out_11(merge_1_out_11));
  register register_1 (.in_1(in_1), .in_2(in_4), .in_3(merge_1_out_11), .out_4(out_13));
endmodule

module _0 (
  input  in_1,
  output [7:0] out_2
);


  assign out_2 = {8{1'b0}};
endmodule

module _1 (
  input  in_1,
  output [7:0] out_2
);

  and and_1 (out_2[0], 1'b1, in_1);

  assign out_2[7:1] = {7{1'b0}};
endmodule

module merge (
  input  [7:0] in_1,
  input  [7:0] in_2,
  input  [7:0] in_3,
  input  [7:0] in_4,
  input  [7:0] in_5,
  input  [7:0] in_6,
  input  [7:0] in_7,
  input  [7:0] in_8,
  input  [7:0] in_9,
  input  [7:0] in_10,
  output [7:0] out_11
);

  wire or_9_out, or_10_out;

  or or_1 (out_11[0], in_1[0], in_2[0], in_3[0], in_4[0], in_10[0], in_5[0], in_6[0], in_7[0], in_8[0]);
  or or_2 (out_11[1], in_1[1], in_2[1], in_3[1], in_4[1], in_5[1], in_6[1], in_7[1], in_8[1]);
  or or_3 (out_11[2], in_1[2], in_3[2], in_4[2], in_5[2], in_6[2], in_7[2], in_8[2]);
  or or_4 (out_11[3], in_1[3], in_9[3], in_10[3]);
  buf or_5 (out_11[4], in_1[4]);  // OR_Gate
  buf or_6 (out_11[5], in_1[5]);  // OR_Gate
  buf or_7 (out_11[6], in_1[6]);  // OR_Gate
  buf or_8 (out_11[7], in_1[7]);  // OR_Gate
  // OR_Gate or_9 has open pins: out=or_9_out
  // OR_Gate or_10 has open pins: out=or_10_out
endmodule

module register (
  input  in_1,
  input  in_2,
  input  [7:0] in_3,
  output [7:0] out_4
);

  wire and_1_out;

  and and_1 (and_1_out, in_1, in_2);
  D_Flip_Flop d_ff_1 (.clk(and_1_out), .D(in_3[0]), .Q(out_4[0]));  // open: Qn, preset, en, reset
  D_Flip_Flop d_ff_2 (.clk(and_1_out), .D(in_3[1]), .Q(out_4[1]));  // open: Qn, preset, en, reset
  D_Flip_Flop d_ff_3 (.clk(and_1_out), .D(in_3[2]), .Q(out_4[2]));  // open: Qn, preset, en, reset
  D_Flip_Flop d_ff_4 (.clk(and_1_out), .D(in_3[3]), .Q(out_4[3]));  // open: Qn, preset, en, reset
  D_Flip_Flop d_ff_5 (.clk(and_1_out), .D(in_3[4]), .Q(out_4[4]));  // open: Qn, preset, en, reset
  D_Flip_Flop d_ff_6 (.clk(and_1_out), .D(in_3[5]), .Q(out_4[5]));  // open: Qn, preset, en, reset
  D_Flip_Flop d_ff_7 (.clk(and_1_out), .D(in_3[6]), .Q(out_4[6]));  // open: Qn, preset, en, reset
  D_Flip_Flop d_ff_8 (.clk(and_1_out), .D(in_3[7]), .Q(out_4[7]));  // open: Qn, preset, en, reset
endmodule

module _2 (
  input  in_1,
  output [7:0] out_2
);

  and and_1 (out_2[1], 1'b1, in_1);

  assign {out_2[7:2], out_2[0]} = {7{1'b0}};
endmodule

module _3 (
  input  in_1,
  output [7:0] out_2
);

  and and_1 (out_2[1], 1'b1, in_1);

  assign {out_2[7:2], out_2[0]} = {{6{1'b0}}, out_2[1]};
endmodule

module _4 (
  input  in_1,
  output [7:0] out_2
);

  and and_1 (out_2[2], 1'b1, in_1);

  assign {out_2[7:3], out_2[1:0]} = {7{1'b0}};
endmodule

module _5 (
  input  in_1,
  output [7:0] out_2
);

  and and_1 (out_2[2], 1'b1, in_1);

  assign {out_2[7:3], out_2[1:0]} = {{6{1'b0}}, out_2[2]};
endmodule

module _6 (
  input  in_1,
  output [7:0] out_2
);

  and and_1 (out_2[2], 1'b1, in_1);

  assign {out_2[7:3], out_2[1:0]} = {{5{1'b0}}, out_2[2], 1'b0};
endmodule

module _7 (
  input  in_1,
  output [7:0] out_2
);

  and and_1 (out_2[2], 1'b1, in_1);

  assign {out_2[7:3], out_2[1:0]} = {{5{1'b0}}, {2{out_2[2]}}};
endmodule

module _8 (
  input  in_1,
  output [7:0] out_2
);

  and and_1 (out_2[3], 1'b1, in_1);

  assign {out_2[7:4], out_2[2:0]} = {7{1'b0}};
endmodule

module _9 (
  input  in_1,
  output [7:0] out_2
);

  and and_1 (out_2[3], 1'b1, in_1);

  assign {out_2[7:4], out_2[2:0]} = {{6{1'b0}}, out_2[3]};
endmodule
