// Logisim project InstructionCache.circ as structural Verilog: 5 circuits, main circuit main
module main (
  input  Clock,
  input  [7:0] Input,
  input  R_W,
  input  [3:0] Address,
  output [7:0] out_5
);

  wire and_1_out, and_2_out, and_3_out, and_4_out, and_5_out, and_6_out, and_7_out, and_8_out, and_9_out,
       and_10_out, and_11_out, and_12_out, and_13_out, and_14_out, and_15_out, and_16_out, Byte_0_out_11,
       Byte_0_out_12, Byte_0_out_13, Byte_0_out_14, Byte_0_out_15, Byte_0_out_16, Byte_0_out_17,
       Byte_0_out_18, Byte_1_out_11, Byte_1_out_12, Byte_1_out_13, Byte_1_out_14, Byte_1_out_15,
       Byte_1_out_16, Byte_1_out_17, Byte_1_out_18, Byte_2_out_11, Byte_2_out_12, Byte_2_out_13,
       Byte_2_out_14, Byte_2_out_15, Byte_2_out_16, Byte_2_out_17, Byte_2_out_18, Byte_3_out_11,
       Byte_3_out_12, Byte_3_out_13, Byte_3_out_14, Byte_3_out_15, Byte_3_out_16, Byte_3_out_17,
       Byte_3_out_18, Byte_4_out_11, Byte_4_out_12, Byte_4_out_13, Byte_4_out_14, Byte_4_out_15,
       Byte_4_out_16, Byte_4_out_17, Byte_4_out_18, Byte_5_out_11, Byte_5_out_12, Byte_5_out_13,
       Byte_5_out_14, Byte_5_out_15, Byte_5_out_16, Byte_5_out_17, Byte_5_out_18, Byte_6_out_11,
       Byte_6_out_12, Byte_6_out_13, Byte_6_out_14, Byte_6_out_15, Byte_6_out_16, Byte_6_out_17,
       Byte_6_out_18, Byte_7_out_11, Byte_7_out_12, Byte_7_out_13, Byte_7_out_14, Byte_7_out_15,
       Byte_7_out_16, Byte_7_out_17, Byte_7_out_18, Byte_8_out_11, Byte_8_out_12, Byte_8_out_13,
       Byte_8_out_14, Byte_8_out_15, Byte_8_out_16, Byte_8_out_17, Byte_8_out_18, Byte_9_out_11,
       Byte_9_out_12, Byte_9_out_13, Byte_9_out_14, Byte_9_out_15, Byte_9_out_16, Byte_9_out_17,
       Byte_9_out_18, Byte_10_out_11, Byte_10_out_12, Byte_10_out_13, Byte_10_out_14, Byte_10_out_15,
       Byte_10_out_16, Byte_10_out_17, Byte_10_out_18, Byte_11_out_11, Byte_11_out_12, Byte_11_out_13,
       Byte_11_out_14, Byte_11_out_15, Byte_11_out_16, Byte_11_out_17, Byte_11_out_18, Byte_12_out_11,
       Byte_12_out_12, Byte_12_out_13, Byte_12_out_14, Byte_12_out_15, Byte_12_out_16, Byte_12_out_17,
       Byte_12_out_18, Byte_13_out_11, Byte_13_out_12, Byte_13_out_13, Byte_13_out_14, Byte_13_out_15,
       Byte_13_out_16, Byte_13_out_17, Byte_13_out_18, Byte_14_out_11, Byte_14_out_12, Byte_14_out_13,
       Byte_14_out_14, Byte_14_out_15, Byte_14_out_16, Byte_14_out_17, Byte_14_out_18, Byte_15_out_11,
       Byte_15_out_12, Byte_15_out_13, Byte_15_out_14, Byte_15_out_15, Byte_15_out_16, Byte_15_out_17,
       Byte_15_out_18, n8_bit_condition_1_out_10, n8_bit_condition_1_out_11, n8_bit_condition_1_out_12,
       n8_bit_condition_1_out_13, n8_bit_condition_1_out_14, n8_bit_condition_1_out_15,
       n8_bit_condition_1_out_16, n8_bit_condition_1_out_17, n8_bit_condition_2_out_10,
       n8_bit_condition_2_out_11, n8_bit_condition_2_out_12, n8_bit_condition_2_out_13,
       n8_bit_condition_2_out_14, n8_bit_condition_2_out_15, n8_bit_condition_2_out_16,
       n8_bit_condition_2_out_17, n8_bit_condition_3_out_10, n8_bit_condition_3_out_11,
       n8_bit_condition_3_out_12, n8_bit_condition_3_out_13, n8_bit_condition_3_out_14,
       n8_bit_condition_3_out_15, n8_bit_condition_3_out_16, n8_bit_condition_3_out_17,
       n8_bit_condition_4_out_10, n8_bit_condition_4_out_11, n8_bit_condition_4_out_12,
       n8_bit_condition_4_out_13, n8_bit_condition_4_out_14, n8_bit_condition_4_out_15,
       n8_bit_condition_4_out_16, n8_bit_condition_4_out_17, n8_bit_condition_9_out_10,
       n8_bit_condition_9_out_11, n8_bit_condition_9_out_12, n8_bit_condition_9_out_13,
       n8_bit_condition_9_out_14, n8_bit_condition_9_out_15, n8_bit_condition_9_out_16,
       n8_bit_condition_9_out_17, n8_bit_condition_10_out_10, n8_bit_condition_10_out_11,
       n8_bit_condition_10_out_12, n8_bit_condition_10_out_13, n8_bit_condition_10_out_14,
       n8_bit_condition_10_out_15, n8_bit_condition_10_out_16, n8_bit_condition_10_out_17,
       n8_bit_condition_11_out_10, n8_bit_condition_11_out_11, n8_bit_condition_11_out_12,
       n8_bit_condition_11_out_13, n8_bit_condition_11_out_14, n8_bit_condition_11_out_15,
       n8_bit_condition_11_out_16, n8_bit_condition_11_out_17, n8_bit_condition_12_out_10,
       n8_bit_condition_12_out_11, n8_bit_condition_12_out_12, n8_bit_condition_12_out_13,
       n8_bit_condition_12_out_14, n8_bit_condition_12_out_15, n8_bit_condition_12_out_16,
       n8_bit_condition_12_out_17, n8_bit_condition_17_out_10, n8_bit_condition_17_out_11,
       n8_bit_condition_17_out_12, n8_bit_condition_17_out_13, n8_bit_condition_17_out_14,
       n8_bit_condition_17_out_15, n8_bit_condition_17_out_16, n8_bit_condition_17_out_17,
       n8_bit_condition_18_out_10, n8_bit_condition_18_out_11, n8_bit_condition_18_out_12,
       n8_bit_condition_18_out_13, n8_bit_condition_18_out_14, n8_bit_condition_18_out_15,
       n8_bit_condition_18_out_16, n8_bit_condition_18_out_17, n8_bit_condition_19_out_10,
       n8_bit_condition_19_out_11, n8_bit_condition_19_out_12, n8_bit_condition_19_out_13,
       n8_bit_condition_19_out_14, n8_bit_condition_19_out_15, n8_bit_condition_19_out_16,
       n8_bit_condition_19_out_17, n8_bit_condition_20_out_10, n8_bit_condition_20_out_11,
       n8_bit_condition_20_out_12, n8_bit_condition_20_out_13, n8_bit_condition_20_out_14,
       n8_bit_condition_20_out_15, n8_bit_condition_20_out_16, n8_bit_condition_20_out_17,
       n8_bit_condition_25_out_10, n8_bit_condition_25_out_11, n8_bit_condition_25_out_12,
       n8_bit_condition_25_out_13, n8_bit_condition_25_out_14, n8_bit_condition_25_out_15,
       n8_bit_condition_25_out_16, n8_bit_condition_25_out_17, n8_bit_condition_26_out_10,
       n8_bit_condition_26_out_11, n8_bit_condition_26_out_12, n8_bit_condition_26_out_13,
       n8_bit_condition_26_out_14, n8_bit_condition_26_out_15, n8_bit_condition_26_out_16,
       n8_bit_condition_26_out_17, n8_bit_condition_27_out_10, n8_bit_condition_27_out_11,
       n8_bit_condition_27_out_12, n8_bit_condition_27_out_13, n8_bit_condition_27_out_14,
       n8_bit_condition_27_out_15, n8_bit_condition_27_out_16, n8_bit_condition_27_out_17,
       n8_bit_condition_28_out_10, n8_bit_condition_28_out_11, n8_bit_condition_28_out_12,
       n8_bit_condition_28_out_13, n8_bit_condition_28_out_14, n8_bit_condition_28_out_15,
       n8_bit_condition_28_out_16, n8_bit_condition_28_out_17, not_1_out, not_2_out, not_3_out, not_4_out,
       not_5_out, not_6_out, not_7_out, not_8_out, not_9_out, not_10_out, not_11_out, not_12_out, not_13_out,
       not_14_out, not_15_out, not_16_out, not_17_out, not_18_out, not_19_out, not_20_out, not_21_out,
       not_22_out, not_23_out, not_24_out, not_25_out, not_26_out, not_27_out, not_28_out, not_29_out,
       not_30_out, not_31_out, not_32_out, not_33_out, select_byte_for_r_w_1_read,
       select_byte_for_r_w_1_write, select_byte_for_r_w_2_read, select_byte_for_r_w_2_write,
       select_byte_for_r_w_3_read, select_byte_for_r_w_3_write, select_byte_for_r_w_4_read,
       select_byte_for_r_w_4_write, select_byte_for_r_w_5_read, select_byte_for_r_w_5_write,
       select_byte_for_r_w_6_read, select_byte_for_r_w_6_write, select_byte_for_r_w_7_read,
       select_byte_for_r_w_7_write, select_byte_for_r_w_8_read, select_byte_for_r_w_8_write,
       select_byte_for_r_w_9_read, select_byte_for_r_w_9_write, select_byte_for_r_w_10_read,
       select_byte_for_r_w_10_write, select_byte_for_r_w_11_read, select_byte_for_r_w_11_write,
       select_byte_for_r_w_12_read, select_byte_for_r_w_12_write, select_byte_for_r_w_13_read,
       select_byte_for_r_w_13_write, select_byte_for_r_w_14_read, select_byte_for_r_w_14_write,
       select_byte_for_r_w_15_read, select_byte_for_r_w_15_write, select_byte_for_r_w_16_read,
       select_byte_for_r_w_16_write;
  wire [7:0] data_register_1_into_cache, n8_bit_condition_5_out_10, n8_bit_condition_6_out_10,
       n8_bit_condition_7_out_10, n8_bit_condition_8_out_10, n8_bit_condition_13_out_10,
       n8_bit_condition_14_out_10, n8_bit_condition_15_out_10, n8_bit_condition_16_out_10,
       n8_bit_condition_21_out_10, n8_bit_condition_22_out_10, n8_bit_condition_23_out_10,
       n8_bit_condition_24_out_10, n8_bit_condition_29_out_10, n8_bit_condition_30_out_10,
       n8_bit_condition_31_out_10, n8_bit_condition_32_out_10, or_1_out, or_2_out, or_3_out, or_4_out,
       or_5_out, or_6_out, or_7_out, or_8_out, or_9_out, or_10_out, or_11_out, or_12_out, or_13_out;

  not not_1 (not_1_out, Address[0]);
  not not_2 (not_2_out, Address[1]);
  and and_1 (and_1_out, not_1_out, not_2_out, not_3_out, not_4_out);
  not not_3 (not_3_out, Address[2]);
  not not_4 (not_4_out, Address[3]);
  not not_5 (not_5_out, Address[1]);
  and and_2 (and_2_out, Address[0], not_5_out, not_6_out, not_7_out);
  not not_6 (not_6_out, Address[2]);
  not not_7 (not_7_out, Address[3]);
  not not_8 (not_8_out, Address[0]);
  and and_3 (and_3_out, not_8_out, Address[1], not_9_out, not_10_out);
  not not_9 (not_9_out, Address[2]);
  not not_10 (not_10_out, Address[3]);
  and and_4 (and_4_out, Address[0], Address[1], not_11_out, not_12_out);
  not not_11 (not_11_out, Address[2]);
  not not_12 (not_12_out, Address[3]);
  Select_Byte_for_R_W select_byte_for_r_w_1 (
    .Read(select_byte_for_r_w_1_read), .Write(select_byte_for_r_w_1_write), .Selected(and_1_out), .R_W(R_W));
  Select_Byte_for_R_W select_byte_for_r_w_2 (
    .Read(select_byte_for_r_w_2_read), .Write(select_byte_for_r_w_2_write), .Selected(and_2_out), .R_W(R_W));
  Select_Byte_for_R_W select_byte_for_r_w_3 (
    .Read(select_byte_for_r_w_3_read), .Write(select_byte_for_r_w_3_write), .Selected(and_3_out), .R_W(R_W));
  Select_Byte_for_R_W select_byte_for_r_w_4 (
    .Read(select_byte_for_r_w_4_read), .Write(select_byte_for_r_w_4_write), .Selected(and_4_out), .R_W(R_W));
  _8_bit_Condition_Gate u_8_bit_condition_1 (
    .in_2(data_register_1_into_cache[0]), .in_3(data_register_1_into_cache[1]),
    .in_4(data_register_1_into_cache[2]), .in_5(data_register_1_into_cache[3]),
    .in_6(data_register_1_into_cache[4]), .in_7(data_register_1_into_cache[5]),
    .in_8(data_register_1_into_cache[6]), .in_9(data_register_1_into_cache[7]),
    .out_10(n8_bit_condition_1_out_10), .out_11(n8_bit_condition_1_out_11),
    .out_12(n8_bit_condition_1_out_12), .out_13(n8_bit_condition_1_out_13),
    .out_14(n8_bit_condition_1_out_14), .out_15(n8_bit_condition_1_out_15),
    .out_16(n8_bit_condition_1_out_16), .out_17(n8_bit_condition_1_out_17),
    .Condition(select_byte_for_r_w_1_write));
  _8_bit_Condition_Gate u_8_bit_condition_2 (
    .in_2(data_register_1_into_cache[0]), .in_3(data_register_1_into_cache[1]),
    .in_4(data_register_1_into_cache[2]), .in_5(data_register_1_into_cache[3]),
    .in_6(data_register_1_into_cache[4]), .in_7(data_register_1_into_cache[5]),
    .in_8(data_register_1_into_cache[6]), .in_9(data_register_1_into_cache[7]),
    .out_10(n8_bit_condition_2_out_10), .out_11(n8_bit_condition_2_out_11),
    .out_12(n8_bit_condition_2_out_12), .out_13(n8_bit_condition_2_out_13),
    .out_14(n8_bit_condition_2_out_14), .out_15(n8_bit_condition_2_out_15),
    .out_16(n8_bit_condition_2_out_16), .out_17(n8_bit_condition_2_out_17),
    .Condition(select_byte_for_r_w_2_write));
  Byte Byte_0 (
    .in_3(n8_bit_condition_1_out_10), .in_4(n8_bit_condition_1_out_11), .in_5(n8_bit_condition_1_out_12),
    .in_6(n8_bit_condition_1_out_13), .in_7(n8_bit_condition_1_out_14), .in_8(n8_bit_condition_1_out_15),
    .in_9(n8_bit_condition_1_out_16), .in_10(n8_bit_condition_1_out_17), .out_11(Byte_0_out_11),
    .out_12(Byte_0_out_12), .out_13(Byte_0_out_13), .out_14(Byte_0_out_14), .out_15(Byte_0_out_15),
    .out_16(Byte_0_out_16), .out_17(Byte_0_out_17), .out_18(Byte_0_out_18),
    .R_W(select_byte_for_r_w_1_write), .Clock(Clock));
  Byte Byte_1 (
    .in_3(n8_bit_condition_2_out_10), .in_4(n8_bit_condition_2_out_11), .in_5(n8_bit_condition_2_out_12),
    .in_6(n8_bit_condition_2_out_13), .in_7(n8_bit_condition_2_out_14), .in_8(n8_bit_condition_2_out_15),
    .in_9(n8_bit_condition_2_out_16), .in_10(n8_bit_condition_2_out_17), .out_11(Byte_1_out_11),
    .out_12(Byte_1_out_12), .out_13(Byte_1_out_13), .out_14(Byte_1_out_14), .out_15(Byte_1_out_15),
    .out_16(Byte_1_out_16), .out_17(Byte_1_out_17), .out_18(Byte_1_out_18),
    .R_W(select_byte_for_r_w_2_write), .Clock(Clock));
  _8_bit_Condition_Gate u_8_bit_condition_3 (
    .in_2(data_register_1_into_cache[0]), .in_3(data_register_1_into_cache[1]),
    .in_4(data_register_1_into_cache[2]), .in_5(data_register_1_into_cache[3]),
    .in_6(data_register_1_into_cache[4]), .in_7(data_register_1_into_cache[5]),
    .in_8(data_register_1_into_cache[6]), .in_9(data_register_1_into_cache[7]),
    .out_10(n8_bit_condition_3_out_10), .out_11(n8_bit_condition_3_out_11),
    .out_12(n8_bit_condition_3_out_12), .out_13(n8_bit_condition_3_out_13),
    .out_14(n8_bit_condition_3_out_14), .out_15(n8_bit_condition_3_out_15),
    .out_16(n8_bit_condition_3_out_16), .out_17(n8_bit_condition_3_out_17),
    .Condition(select_byte_for_r_w_3_write));
  _8_bit_Condition_Gate u_8_bit_condition_4 (
    .in_2(data_register_1_into_cache[0]), .in_3(data_register_1_into_cache[1]),
    .in_4(data_register_1_into_cache[2]), .in_5(data_register_1_into_cache[3]),
    .in_6(data_register_1_into_cache[4]), .in_7(data_register_1_into_cache[5]),
    .in_8(data_register_1_into_cache[6]), .in_9(data_register_1_into_cache[7]),
    .out_10(n8_bit_condition_4_out_10), .out_11(n8_bit_condition_4_out_11),
    .out_12(n8_bit_condition_4_out_12), .out_13(n8_bit_condition_4_out_13),
    .out_14(n8_bit_condition_4_out_14), .out_15(n8_bit_condition_4_out_15),
    .out_16(n8_bit_condition_4_out_16), .out_17(n8_bit_condition_4_out_17),
    .Condition(select_byte_for_r_w_4_write));
  _8_bit_Condition_Gate u_8_bit_condition_5 (
    .in_2(Byte_0_out_11), .in_3(Byte_0_out_12), .in_4(Byte_0_out_13), .in_5(Byte_0_out_14),
    .in_6(Byte_0_out_15), .in_7(Byte_0_out_16), .in_8(Byte_0_out_17), .in_9(Byte_0_out_18),
    .out_10(n8_bit_condition_5_out_10[0]), .out_11(n8_bit_condition_5_out_10[1]),
    .out_12(n8_bit_condition_5_out_10[2]), .out_13(n8_bit_condition_5_out_10[3]),
    .out_14(n8_bit_condition_5_out_10[4]), .out_15(n8_bit_condition_5_out_10[5]),
    .out_16(n8_bit_condition_5_out_10[6]), .out_17(n8_bit_condition_5_out_10[7]),
    .Condition(select_byte_for_r_w_1_read));
  _8_bit_Condition_Gate u_8_bit_condition_6 (
    .in_2(Byte_1_out_11), .in_3(Byte_1_out_12), .in_4(Byte_1_out_13), .in_5(Byte_1_out_14),
    .in_6(Byte_1_out_15), .in_7(Byte_1_out_16), .in_8(Byte_1_out_17), .in_9(Byte_1_out_18),
    .out_10(n8_bit_condition_6_out_10[0]), .out_11(n8_bit_condition_6_out_10[1]),
    .out_12(n8_bit_condition_6_out_10[2]), .out_13(n8_bit_condition_6_out_10[3]),
    .out_14(n8_bit_condition_6_out_10[4]), .out_15(n8_bit_condition_6_out_10[5]),
    .out_16(n8_bit_condition_6_out_10[6]), .out_17(n8_bit_condition_6_out_10[7]),
    .Condition(select_byte_for_r_w_2_read));
  Byte Byte_2 (
    .in_3(n8_bit_condition_3_out_10), .in_4(n8_bit_condition_3_out_11), .in_5(n8_bit_condition_3_out_12),
    .in_6(n8_bit_condition_3_out_13), .in_7(n8_bit_condition_3_out_14), .in_8(n8_bit_condition_3_out_15),
    .in_9(n8_bit_condition_3_out_16), .in_10(n8_bit_condition_3_out_17), .out_11(Byte_2_out_11),
    .out_12(Byte_2_out_12), .out_13(Byte_2_out_13), .out_14(Byte_2_out_14), .out_15(Byte_2_out_15),
    .out_16(Byte_2_out_16), .out_17(Byte_2_out_17), .out_18(Byte_2_out_18),
    .R_W(select_byte_for_r_w_3_write), .Clock(Clock));
  _8_bit_Condition_Gate u_8_bit_condition_7 (
    .in_2(Byte_2_out_11), .in_3(Byte_2_out_12), .in_4(Byte_2_out_13), .in_5(Byte_2_out_14),
    .in_6(Byte_2_out_15), .in_7(Byte_2_out_16), .in_8(Byte_2_out_17), .in_9(Byte_2_out_18),
    .out_10(n8_bit_condition_7_out_10[0]), .out_11(n8_bit_condition_7_out_10[1]),
    .out_12(n8_bit_condition_7_out_10[2]), .out_13(n8_bit_condition_7_out_10[3]),
    .out_14(n8_bit_condition_7_out_10[4]), .out_15(n8_bit_condition_7_out_10[5]),
    .out_16(n8_bit_condition_7_out_10[6]), .out_17(n8_bit_condition_7_out_10[7]),
    .Condition(select_byte_for_r_w_3_read));
  _8_bit_Condition_Gate u_8_bit_condition_8 (
    .in_2(Byte_3_out_11), .in_3(Byte_3_out_12), .in_4(Byte_3_out_13), .in_5(Byte_3_out_14),
    .in_6(Byte_3_out_15), .in_7(Byte_3_out_16), .in_8(Byte_3_out_17), .in_9(Byte_3_out_18),
    .out_10(n8_bit_condition_8_out_10[0]), .out_11(n8_bit_condition_8_out_10[1]),
    .out_12(n8_bit_condition_8_out_10[2]), .out_13(n8_bit_condition_8_out_10[3]),
    .out_14(n8_bit_condition_8_out_10[4]), .out_15(n8_bit_condition_8_out_10[5]),
    .out_16(n8_bit_condition_8_out_10[6]), .out_17(n8_bit_condition_8_out_10[7]),
    .Condition(select_byte_for_r_w_4_read));
  Byte Byte_3 (
    .in_3(n8_bit_condition_4_out_10), .in_4(n8_bit_condition_4_out_11), .in_5(n8_bit_condition_4_out_12),
    .in_6(n8_bit_condition_4_out_13), .in_7(n8_bit_condition_4_out_14), .in_8(n8_bit_condition_4_out_15),
    .in_9(n8_bit_condition_4_out_16), .in_10(n8_bit_condition_4_out_17), .out_11(Byte_3_out_11),
    .out_12(Byte_3_out_12), .out_13(Byte_3_out_13), .out_14(Byte_3_out_14), .out_15(Byte_3_out_15),
    .out_16(Byte_3_out_16), .out_17(Byte_3_out_17), .out_18(Byte_3_out_18),
    .R_W(select_byte_for_r_w_4_write), .Clock(Clock));
  assign or_1_out = n8_bit_condition_5_out_10 | or_2_out;  // OR_Gate or_1, 8 bits wide
  assign or_2_out = n8_bit_condition_6_out_10 | or_3_out;  // OR_Gate or_2, 8 bits wide
  assign or_3_out = n8_bit_condition_7_out_10 | n8_bit_condition_8_out_10;  // OR_Gate or_3, 8 bits wide
  not not_13 (not_13_out, Address[0]);
  not not_14 (not_14_out, Address[1]);
  and and_5 (and_5_out, not_13_out, not_14_out, Address[2], not_15_out);
  not not_15 (not_15_out, Address[3]);
  not not_16 (not_16_out, Address[1]);
  and and_6 (and_6_out, Address[0], not_16_out, Address[2], not_17_out);
  not not_17 (not_17_out, Address[3]);
  not not_18 (not_18_out, Address[0]);
  and and_7 (and_7_out, not_18_out, Address[1], Address[2], not_19_out);
  not not_19 (not_19_out, Address[3]);
  and and_8 (and_8_out, Address[0], Address[1], Address[2], not_20_out);
  not not_20 (not_20_out, Address[3]);
  Select_Byte_for_R_W select_byte_for_r_w_5 (
    .Read(select_byte_for_r_w_5_read), .Write(select_byte_for_r_w_5_write), .Selected(and_5_out), .R_W(R_W));
  Select_Byte_for_R_W select_byte_for_r_w_6 (
    .Read(select_byte_for_r_w_6_read), .Write(select_byte_for_r_w_6_write), .Selected(and_6_out), .R_W(R_W));
  Select_Byte_for_R_W select_byte_for_r_w_7 (
    .Read(select_byte_for_r_w_7_read), .Write(select_byte_for_r_w_7_write), .Selected(and_7_out), .R_W(R_W));
  Select_Byte_for_R_W select_byte_for_r_w_8 (
    .Read(select_byte_for_r_w_8_read), .Write(select_byte_for_r_w_8_write), .Selected(and_8_out), .R_W(R_W));
  assign or_4_out = or_1_out | or_5_out | or_8_out | or_11_out;  // OR_Gate or_4, 8 bits wide
  _8_bit_Condition_Gate u_8_bit_condition_9 (
    .in_2(data_register_1_into_cache[0]), .in_3(data_register_1_into_cache[1]),
    .in_4(data_register_1_into_cache[2]), .in_5(data_register_1_into_cache[3]),
    .in_6(data_register_1_into_cache[4]), .in_7(data_register_1_into_cache[5]),
    .in_8(data_register_1_into_cache[6]), .in_9(data_register_1_into_cache[7]),
    .out_10(n8_bit_condition_9_out_10), .out_11(n8_bit_condition_9_out_11),
    .out_12(n8_bit_condition_9_out_12), .out_13(n8_bit_condition_9_out_13),
    .out_14(n8_bit_condition_9_out_14), .out_15(n8_bit_condition_9_out_15),
    .out_16(n8_bit_condition_9_out_16), .out_17(n8_bit_condition_9_out_17),
    .Condition(select_byte_for_r_w_5_write));
  _8_bit_Condition_Gate u_8_bit_condition_10 (
    .in_2(data_register_1_into_cache[0]), .in_3(data_register_1_into_cache[1]),
    .in_4(data_register_1_into_cache[2]), .in_5(data_register_1_into_cache[3]),
    .in_6(data_register_1_into_cache[4]), .in_7(data_register_1_into_cache[5]),
    .in_8(data_register_1_into_cache[6]), .in_9(data_register_1_into_cache[7]),
    .out_10(n8_bit_condition_10_out_10), .out_11(n8_bit_condition_10_out_11),
    .out_12(n8_bit_condition_10_out_12), .out_13(n8_bit_condition_10_out_13),
    .out_14(n8_bit_condition_10_out_14), .out_15(n8_bit_condition_10_out_15),
    .out_16(n8_bit_condition_10_out_16), .out_17(n8_bit_condition_10_out_17),
    .Condition(select_byte_for_r_w_6_write));
  _8_bit_Condition_Gate u_8_bit_condition_11 (
    .in_2(data_register_1_into_cache[0]), .in_3(data_register_1_into_cache[1]),
    .in_4(data_register_1_into_cache[2]), .in_5(data_register_1_into_cache[3]),
    .in_6(data_register_1_into_cache[4]), .in_7(data_register_1_into_cache[5]),
    .in_8(data_register_1_into_cache[6]), .in_9(data_register_1_into_cache[7]),
    .out_10(n8_bit_condition_11_out_10), .out_11(n8_bit_condition_11_out_11),
    .out_12(n8_bit_condition_11_out_12), .out_13(n8_bit_condition_11_out_13),
    .out_14(n8_bit_condition_11_out_14), .out_15(n8_bit_condition_11_out_15),
    .out_16(n8_bit_condition_11_out_16), .out_17(n8_bit_condition_11_out_17),
    .Condition(select_byte_for_r_w_7_write));
  _8_bit_Condition_Gate u_8_bit_condition_12 (
    .in_2(data_register_1_into_cache[0]), .in_3(data_register_1_into_cache[1]),
    .in_4(data_register_1_into_cache[2]), .in_5(data_register_1_into_cache[3]),
    .in_6(data_register_1_into_cache[4]), .in_7(data_register_1_into_cache[5]),
    .in_8(data_register_1_into_cache[6]), .in_9(data_register_1_into_cache[7]),
    .out_10(n8_bit_condition_12_out_10), .out_11(n8_bit_condition_12_out_11),
    .out_12(n8_bit_condition_12_out_12), .out_13(n8_bit_condition_12_out_13),
    .out_14(n8_bit_condition_12_out_14), .out_15(n8_bit_condition_12_out_15),
    .out_16(n8_bit_condition_12_out_16), .out_17(n8_bit_condition_12_out_17),
    .Condition(select_byte_for_r_w_8_write));
  not not_21 (not_21_out, R_W);
  Data_Register data_register_1 (
    .R_W(not_21_out), .Clock(Clock), .External_Output(out_5), .into_Cache(data_register_1_into_cache),
    .External_Input(Input), .from_Cache(or_4_out));
  Byte Byte_4 (
    .in_3(n8_bit_condition_9_out_10), .in_4(n8_bit_condition_9_out_11), .in_5(n8_bit_condition_9_out_12),
    .in_6(n8_bit_condition_9_out_13), .in_7(n8_bit_condition_9_out_14), .in_8(n8_bit_condition_9_out_15),
    .in_9(n8_bit_condition_9_out_16), .in_10(n8_bit_condition_9_out_17), .out_11(Byte_4_out_11),
    .out_12(Byte_4_out_12), .out_13(Byte_4_out_13), .out_14(Byte_4_out_14), .out_15(Byte_4_out_15),
    .out_16(Byte_4_out_16), .out_17(Byte_4_out_17), .out_18(Byte_4_out_18),
    .R_W(select_byte_for_r_w_5_write), .Clock(Clock));
  Byte Byte_5 (
    .in_3(n8_bit_condition_10_out_10), .in_4(n8_bit_condition_10_out_11), .in_5(n8_bit_condition_10_out_12),
    .in_6(n8_bit_condition_10_out_13), .in_7(n8_bit_condition_10_out_14), .in_8(n8_bit_condition_10_out_15),
    .in_9(n8_bit_condition_10_out_16), .in_10(n8_bit_condition_10_out_17), .out_11(Byte_5_out_11),
    .out_12(Byte_5_out_12), .out_13(Byte_5_out_13), .out_14(Byte_5_out_14), .out_15(Byte_5_out_15),
    .out_16(Byte_5_out_16), .out_17(Byte_5_out_17), .out_18(Byte_5_out_18),
    .R_W(select_byte_for_r_w_6_write), .Clock(Clock));
  Byte Byte_6 (
    .in_3(n8_bit_condition_11_out_10), .in_4(n8_bit_condition_11_out_11), .in_5(n8_bit_condition_11_out_12),
    .in_6(n8_bit_condition_11_out_13), .in_7(n8_bit_condition_11_out_14), .in_8(n8_bit_condition_11_out_15),
    .in_9(n8_bit_condition_11_out_16), .in_10(n8_bit_condition_11_out_17), .out_11(Byte_6_out_11),
    .out_12(Byte_6_out_12), .out_13(Byte_6_out_13), .out_14(Byte_6_out_14), .out_15(Byte_6_out_15),
    .out_16(Byte_6_out_16), .out_17(Byte_6_out_17), .out_18(Byte_6_out_18),
    .R_W(select_byte_for_r_w_7_write), .Clock(Clock));
  Byte Byte_7 (
    .in_3(n8_bit_condition_12_out_10), .in_4(n8_bit_condition_12_out_11), .in_5(n8_bit_condition_12_out_12),
    .in_6(n8_bit_condition_12_out_13), .in_7(n8_bit_condition_12_out_14), .in_8(n8_bit_condition_12_out_15),
    .in_9(n8_bit_condition_12_out_16), .in_10(n8_bit_condition_12_out_17), .out_11(Byte_7_out_11),
    .out_12(Byte_7_out_12), .out_13(Byte_7_out_13), .out_14(Byte_7_out_14), .out_15(Byte_7_out_15),
    .out_16(Byte_7_out_16), .out_17(Byte_7_out_17), .out_18(Byte_7_out_18),
    .R_W(select_byte_for_r_w_8_write), .Clock(Clock));
  assign or_5_out = n8_bit_condition_13_out_10 | or_6_out;  // OR_Gate or_5, 8 bits wide
  _8_bit_Condition_Gate u_8_bit_condition_13 (
    .in_2(Byte_4_out_11), .in_3(Byte_4_out_12), .in_4(Byte_4_out_13), .in_5(Byte_4_out_14),
    .in_6(Byte_4_out_15), .in_7(Byte_4_out_16), .in_8(Byte_4_out_17), .in_9(Byte_4_out_18),
    .out_10(n8_bit_condition_13_out_10[0]), .out_11(n8_bit_condition_13_out_10[1]),
    .out_12(n8_bit_condition_13_out_10[2]), .out_13(n8_bit_condition_13_out_10[3]),
    .out_14(n8_bit_condition_13_out_10[4]), .out_15(n8_bit_condition_13_out_10[5]),
    .out_16(n8_bit_condition_13_out_10[6]), .out_17(n8_bit_condition_13_out_10[7]),
    .Condition(select_byte_for_r_w_5_read));
  assign or_6_out = n8_bit_condition_14_out_10 | or_7_out;  // OR_Gate or_6, 8 bits wide
  _8_bit_Condition_Gate u_8_bit_condition_14 (
    .in_2(Byte_5_out_11), .in_3(Byte_5_out_12), .in_4(Byte_5_out_13), .in_5(Byte_5_out_14),
    .in_6(Byte_5_out_15), .in_7(Byte_5_out_16), .in_8(Byte_5_out_17), .in_9(Byte_5_out_18),
    .out_10(n8_bit_condition_14_out_10[0]), .out_11(n8_bit_condition_14_out_10[1]),
    .out_12(n8_bit_condition_14_out_10[2]), .out_13(n8_bit_condition_14_out_10[3]),
    .out_14(n8_bit_condition_14_out_10[4]), .out_15(n8_bit_condition_14_out_10[5]),
    .out_16(n8_bit_condition_14_out_10[6]), .out_17(n8_bit_condition_14_out_10[7]),
    .Condition(select_byte_for_r_w_6_read));
  assign or_7_out = n8_bit_condition_15_out_10 | n8_bit_condition_16_out_10;  // OR_Gate or_7, 8 bits wide
  _8_bit_Condition_Gate u_8_bit_condition_15 (
    .in_2(Byte_6_out_11), .in_3(Byte_6_out_12), .in_4(Byte_6_out_13), .in_5(Byte_6_out_14),
    .in_6(Byte_6_out_15), .in_7(Byte_6_out_16), .in_8(Byte_6_out_17), .in_9(Byte_6_out_18),
    .out_10(n8_bit_condition_15_out_10[0]), .out_11(n8_bit_condition_15_out_10[1]),
    .out_12(n8_bit_condition_15_out_10[2]), .out_13(n8_bit_condition_15_out_10[3]),
    .out_14(n8_bit_condition_15_out_10[4]), .out_15(n8_bit_condition_15_out_10[5]),
    .out_16(n8_bit_condition_15_out_10[6]), .out_17(n8_bit_condition_15_out_10[7]),
    .Condition(select_byte_for_r_w_7_read));
  _8_bit_Condition_Gate u_8_bit_condition_16 (
    .in_2(Byte_7_out_11), .in_3(Byte_7_out_12), .in_4(Byte_7_out_13), .in_5(Byte_7_out_14),
    .in_6(Byte_7_out_15), .in_7(Byte_7_out_16), .in_8(Byte_7_out_17), .in_9(Byte_7_out_18),
    .out_10(n8_bit_condition_16_out_10[0]), .out_11(n8_bit_condition_16_out_10[1]),
    .out_12(n8_bit_condition_16_out_10[2]), .out_13(n8_bit_condition_16_out_10[3]),
    .out_14(n8_bit_condition_16_out_10[4]), .out_15(n8_bit_condition_16_out_10[5]),
    .out_16(n8_bit_condition_16_out_10[6]), .out_17(n8_bit_condition_16_out_10[7]),
    .Condition(select_byte_for_r_w_8_read));
  not not_22 (not_22_out, Address[0]);
  not not_23 (not_23_out, Address[1]);
  not not_24 (not_24_out, Address[2]);
  not not_25 (not_25_out, Address[1]);
  not not_26 (not_26_out, Address[2]);
  not not_27 (not_27_out, Address[0]);
  not not_28 (not_28_out, Address[2]);
  not not_29 (not_29_out, Address[2]);
  Select_Byte_for_R_W select_byte_for_r_w_9 (
    .Read(select_byte_for_r_w_9_read), .Write(select_byte_for_r_w_9_write), .Selected(and_9_out), .R_W(R_W));
  and and_9 (and_9_out, not_22_out, not_23_out, not_24_out, Address[3]);
  Select_Byte_for_R_W select_byte_for_r_w_10 (
    .Read(select_byte_for_r_w_10_read), .Write(select_byte_for_r_w_10_write), .Selected(and_10_out), .R_W(R_W));
  and and_10 (and_10_out, Address[0], not_25_out, not_26_out, Address[3]);
  Select_Byte_for_R_W select_byte_for_r_w_11 (
    .Read(select_byte_for_r_w_11_read), .Write(select_byte_for_r_w_11_write), .Selected(and_11_out), .R_W(R_W));
  and and_11 (and_11_out, not_27_out, Address[1], not_28_out, Address[3]);
  Select_Byte_for_R_W select_byte_for_r_w_12 (
    .Read(select_byte_for_r_w_12_read), .Write(select_byte_for_r_w_12_write), .Selected(and_12_out), .R_W(R_W));
  and and_12 (and_12_out, Address[0], Address[1], not_29_out, Address[3]);
  _8_bit_Condition_Gate u_8_bit_condition_17 (
    .in_2(data_register_1_into_cache[0]), .in_3(data_register_1_into_cache[1]),
    .in_4(data_register_1_into_cache[2]), .in_5(data_register_1_into_cache[3]),
    .in_6(data_register_1_into_cache[4]), .in_7(data_register_1_into_cache[5]),
    .in_8(data_register_1_into_cache[6]), .in_9(data_register_1_into_cache[7]),
    .out_10(n8_bit_condition_17_out_10), .out_11(n8_bit_condition_17_out_11),
    .out_12(n8_bit_condition_17_out_12), .out_13(n8_bit_condition_17_out_13),
    .out_14(n8_bit_condition_17_out_14), .out_15(n8_bit_condition_17_out_15),
    .out_16(n8_bit_condition_17_out_16), .out_17(n8_bit_condition_17_out_17),
    .Condition(select_byte_for_r_w_9_write));
  _8_bit_Condition_Gate u_8_bit_condition_18 (
    .in_2(data_register_1_into_cache[0]), .in_3(data_register_1_into_cache[1]),
    .in_4(data_register_1_into_cache[2]), .in_5(data_register_1_into_cache[3]),
    .in_6(data_register_1_into_cache[4]), .in_7(data_register_1_into_cache[5]),
    .in_8(data_register_1_into_cache[6]), .in_9(data_register_1_into_cache[7]),
    .out_10(n8_bit_condition_18_out_10), .out_11(n8_bit_condition_18_out_11),
    .out_12(n8_bit_condition_18_out_12), .out_13(n8_bit_condition_18_out_13),
    .out_14(n8_bit_condition_18_out_14), .out_15(n8_bit_condition_18_out_15),
    .out_16(n8_bit_condition_18_out_16), .out_17(n8_bit_condition_18_out_17),
    .Condition(select_byte_for_r_w_10_write));
  _8_bit_Condition_Gate u_8_bit_condition_19 (
    .in_2(data_register_1_into_cache[0]), .in_3(data_register_1_into_cache[1]),
    .in_4(data_register_1_into_cache[2]), .in_5(data_register_1_into_cache[3]),
    .in_6(data_register_1_into_cache[4]), .in_7(data_register_1_into_cache[5]),
    .in_8(data_register_1_into_cache[6]), .in_9(data_register_1_into_cache[7]),
    .out_10(n8_bit_condition_19_out_10), .out_11(n8_bit_condition_19_out_11),
    .out_12(n8_bit_condition_19_out_12), .out_13(n8_bit_condition_19_out_13),
    .out_14(n8_bit_condition_19_out_14), .out_15(n8_bit_condition_19_out_15),
    .out_16(n8_bit_condition_19_out_16), .out_17(n8_bit_condition_19_out_17),
    .Condition(select_byte_for_r_w_11_write));
  _8_bit_Condition_Gate u_8_bit_condition_20 (
    .in_2(data_register_1_into_cache[0]), .in_3(data_register_1_into_cache[1]),
    .in_4(data_register_1_into_cache[2]), .in_5(data_register_1_into_cache[3]),
    .in_6(data_register_1_into_cache[4]), .in_7(data_register_1_into_cache[5]),
    .in_8(data_register_1_into_cache[6]), .in_9(data_register_1_into_cache[7]),
    .out_10(n8_bit_condition_20_out_10), .out_11(n8_bit_condition_20_out_11),
    .out_12(n8_bit_condition_20_out_12), .out_13(n8_bit_condition_20_out_13),
    .out_14(n8_bit_condition_20_out_14), .out_15(n8_bit_condition_20_out_15),
    .out_16(n8_bit_condition_20_out_16), .out_17(n8_bit_condition_20_out_17),
    .Condition(select_byte_for_r_w_12_write));
  Byte Byte_8 (
    .in_3(n8_bit_condition_17_out_10), .in_4(n8_bit_condition_17_out_11), .in_5(n8_bit_condition_17_out_12),
    .in_6(n8_bit_condition_17_out_13), .in_7(n8_bit_condition_17_out_14), .in_8(n8_bit_condition_17_out_15),
    .in_9(n8_bit_condition_17_out_16), .in_10(n8_bit_condition_17_out_17), .out_11(Byte_8_out_11),
    .out_12(Byte_8_out_12), .out_13(Byte_8_out_13), .out_14(Byte_8_out_14), .out_15(Byte_8_out_15),
    .out_16(Byte_8_out_16), .out_17(Byte_8_out_17), .out_18(Byte_8_out_18),
    .R_W(select_byte_for_r_w_9_write), .Clock(Clock));
  Byte Byte_9 (
    .in_3(n8_bit_condition_18_out_10), .in_4(n8_bit_condition_18_out_11), .in_5(n8_bit_condition_18_out_12),
    .in_6(n8_bit_condition_18_out_13), .in_7(n8_bit_condition_18_out_14), .in_8(n8_bit_condition_18_out_15),
    .in_9(n8_bit_condition_18_out_16), .in_10(n8_bit_condition_18_out_17), .out_11(Byte_9_out_11),
    .out_12(Byte_9_out_12), .out_13(Byte_9_out_13), .out_14(Byte_9_out_14), .out_15(Byte_9_out_15),
    .out_16(Byte_9_out_16), .out_17(Byte_9_out_17), .out_18(Byte_9_out_18),
    .R_W(select_byte_for_r_w_10_write), .Clock(Clock));
  Byte Byte_10 (
    .in_3(n8_bit_condition_19_out_10), .in_4(n8_bit_condition_19_out_11), .in_5(n8_bit_condition_19_out_12),
    .in_6(n8_bit_condition_19_out_13), .in_7(n8_bit_condition_19_out_14), .in_8(n8_bit_condition_19_out_15),
    .in_9(n8_bit_condition_19_out_16), .in_10(n8_bit_condition_19_out_17), .out_11(Byte_10_out_11),
    .out_12(Byte_10_out_12), .out_13(Byte_10_out_13), .out_14(Byte_10_out_14), .out_15(Byte_10_out_15),
    .out_16(Byte_10_out_16), .out_17(Byte_10_out_17), .out_18(Byte_10_out_18),
    .R_W(select_byte_for_r_w_11_write), .Clock(Clock));
  Byte Byte_11 (
    .in_3(n8_bit_condition_20_out_10), .in_4(n8_bit_condition_20_out_11), .in_5(n8_bit_condition_20_out_12),
    .in_6(n8_bit_condition_20_out_13), .in_7(n8_bit_condition_20_out_14), .in_8(n8_bit_condition_20_out_15),
    .in_9(n8_bit_condition_20_out_16), .in_10(n8_bit_condition_20_out_17), .out_11(Byte_11_out_11),
    .out_12(Byte_11_out_12), .out_13(Byte_11_out_13), .out_14(Byte_11_out_14), .out_15(Byte_11_out_15),
    .out_16(Byte_11_out_16), .out_17(Byte_11_out_17), .out_18(Byte_11_out_18),
    .R_W(select_byte_for_r_w_12_write), .Clock(Clock));
  _8_bit_Condition_Gate u_8_bit_condition_21 (
    .in_2(Byte_8_out_11), .in_3(Byte_8_out_12), .in_4(Byte_8_out_13), .in_5(Byte_8_out_14),
    .in_6(Byte_8_out_15), .in_7(Byte_8_out_16), .in_8(Byte_8_out_17), .in_9(Byte_8_out_18),
    .out_10(n8_bit_condition_21_out_10[0]), .out_11(n8_bit_condition_21_out_10[1]),
    .out_12(n8_bit_condition_21_out_10[2]), .out_13(n8_bit_condition_21_out_10[3]),
    .out_14(n8_bit_condition_21_out_10[4]), .out_15(n8_bit_condition_21_out_10[5]),
    .out_16(n8_bit_condition_21_out_10[6]), .out_17(n8_bit_condition_21_out_10[7]),
    .Condition(select_byte_for_r_w_9_read));
  _8_bit_Condition_Gate u_8_bit_condition_22 (
    .in_2(Byte_9_out_11), .in_3(Byte_9_out_12), .in_4(Byte_9_out_13), .in_5(Byte_9_out_14),
    .in_6(Byte_9_out_15), .in_7(Byte_9_out_16), .in_8(Byte_9_out_17), .in_9(Byte_9_out_18),
    .out_10(n8_bit_condition_22_out_10[0]), .out_11(n8_bit_condition_22_out_10[1]),
    .out_12(n8_bit_condition_22_out_10[2]), .out_13(n8_bit_condition_22_out_10[3]),
    .out_14(n8_bit_condition_22_out_10[4]), .out_15(n8_bit_condition_22_out_10[5]),
    .out_16(n8_bit_condition_22_out_10[6]), .out_17(n8_bit_condition_22_out_10[7]),
    .Condition(select_byte_for_r_w_10_read));
  _8_bit_Condition_Gate u_8_bit_condition_23 (
    .in_2(Byte_10_out_11), .in_3(Byte_10_out_12), .in_4(Byte_10_out_13), .in_5(Byte_10_out_14),
    .in_6(Byte_10_out_15), .in_7(Byte_10_out_16), .in_8(Byte_10_out_17), .in_9(Byte_10_out_18),
    .out_10(n8_bit_condition_23_out_10[0]), .out_11(n8_bit_condition_23_out_10[1]),
    .out_12(n8_bit_condition_23_out_10[2]), .out_13(n8_bit_condition_23_out_10[3]),
    .out_14(n8_bit_condition_23_out_10[4]), .out_15(n8_bit_condition_23_out_10[5]),
    .out_16(n8_bit_condition_23_out_10[6]), .out_17(n8_bit_condition_23_out_10[7]),
    .Condition(select_byte_for_r_w_11_read));
  _8_bit_Condition_Gate u_8_bit_condition_24 (
    .in_2(Byte_11_out_11), .in_3(Byte_11_out_12), .in_4(Byte_11_out_13), .in_5(Byte_11_out_14),
    .in_6(Byte_11_out_15), .in_7(Byte_11_out_16), .in_8(Byte_11_out_17), .in_9(Byte_11_out_18),
    .out_10(n8_bit_condition_24_out_10[0]), .out_11(n8_bit_condition_24_out_10[1]),
    .out_12(n8_bit_condition_24_out_10[2]), .out_13(n8_bit_condition_24_out_10[3]),
    .out_14(n8_bit_condition_24_out_10[4]), .out_15(n8_bit_condition_24_out_10[5]),
    .out_16(n8_bit_condition_24_out_10[6]), .out_17(n8_bit_condition_24_out_10[7]),
    .Condition(select_byte_for_r_w_12_read));
  assign or_8_out = n8_bit_condition_21_out_10 | or_9_out;  // OR_Gate or_8, 8 bits wide
  assign or_9_out = n8_bit_condition_22_out_10 | or_10_out;  // OR_Gate or_9, 8 bits wide
  assign or_10_out = n8_bit_condition_23_out_10 | n8_bit_condition_24_out_10;  // OR_Gate or_10, 8 bits wide
  not not_30 (not_30_out, Address[0]);
  not not_31 (not_31_out, Address[1]);
  and and_13 (and_13_out, not_30_out, not_31_out, Address[2], Address[3]);
  not not_32 (not_32_out, Address[1]);
  and and_14 (and_14_out, Address[0], not_32_out, Address[2], Address[3]);
  not not_33 (not_33_out, Address[0]);
  and and_15 (and_15_out, not_33_out, Address[1], Address[2]);
  and and_16 (and_16_out, Address[0], Address[1], Address[2], Address[3]);
  Select_Byte_for_R_W select_byte_for_r_w_13 (
    .Read(select_byte_for_r_w_13_read), .Write(select_byte_for_r_w_13_write), .Selected(and_13_out), .R_W(R_W));
  Select_Byte_for_R_W select_byte_for_r_w_14 (
    .Read(select_byte_for_r_w_14_read), .Write(select_byte_for_r_w_14_write), .Selected(and_14_out), .R_W(R_W));
  Select_Byte_for_R_W select_byte_for_r_w_15 (
    .Read(select_byte_for_r_w_15_read), .Write(select_byte_for_r_w_15_write), .Selected(and_15_out), .R_W(R_W));
  Select_Byte_for_R_W select_byte_for_r_w_16 (
    .Read(select_byte_for_r_w_16_read), .Write(select_byte_for_r_w_16_write), .Selected(and_16_out), .R_W(R_W));
  _8_bit_Condition_Gate u_8_bit_condition_25 (
    .in_2(data_register_1_into_cache[0]), .in_3(data_register_1_into_cache[1]),
    .in_4(data_register_1_into_cache[2]), .in_5(data_register_1_into_cache[3]),
    .in_6(data_register_1_into_cache[4]), .in_7(data_register_1_into_cache[5]),
    .in_8(data_register_1_into_cache[6]), .in_9(data_register_1_into_cache[7]),
    .out_10(n8_bit_condition_25_out_10), .out_11(n8_bit_condition_25_out_11),
    .out_12(n8_bit_condition_25_out_12), .out_13(n8_bit_condition_25_out_13),
    .out_14(n8_bit_condition_25_out_14), .out_15(n8_bit_condition_25_out_15),
    .out_16(n8_bit_condition_25_out_16), .out_17(n8_bit_condition_25_out_17),
    .Condition(select_byte_for_r_w_13_write));
  _8_bit_Condition_Gate u_8_bit_condition_26 (
    .in_2(data_register_1_into_cache[0]), .in_3(data_register_1_into_cache[1]),
    .in_4(data_register_1_into_cache[2]), .in_5(data_register_1_into_cache[3]),
    .in_6(data_register_1_into_cache[4]), .in_7(data_register_1_into_cache[5]),
    .in_8(data_register_1_into_cache[6]), .in_9(data_register_1_into_cache[7]),
    .out_10(n8_bit_condition_26_out_10), .out_11(n8_bit_condition_26_out_11),
    .out_12(n8_bit_condition_26_out_12), .out_13(n8_bit_condition_26_out_13),
    .out_14(n8_bit_condition_26_out_14), .out_15(n8_bit_condition_26_out_15),
    .out_16(n8_bit_condition_26_out_16), .out_17(n8_bit_condition_26_out_17),
    .Condition(select_byte_for_r_w_14_write));
  _8_bit_Condition_Gate u_8_bit_condition_27 (
    .in_2(data_register_1_into_cache[0]), .in_3(data_register_1_into_cache[1]),
    .in_4(data_register_1_into_cache[2]), .in_5(data_register_1_into_cache[3]),
    .in_6(data_register_1_into_cache[4]), .in_7(data_register_1_into_cache[5]),
    .in_8(data_register_1_into_cache[6]), .in_9(data_register_1_into_cache[7]),
    .out_10(n8_bit_condition_27_out_10), .out_11(n8_bit_condition_27_out_11),
    .out_12(n8_bit_condition_27_out_12), .out_13(n8_bit_condition_27_out_13),
    .out_14(n8_bit_condition_27_out_14), .out_15(n8_bit_condition_27_out_15),
    .out_16(n8_bit_condition_27_out_16), .out_17(n8_bit_condition_27_out_17),
    .Condition(select_byte_for_r_w_15_write));
  _8_bit_Condition_Gate u_8_bit_condition_28 (
    .in_2(data_register_1_into_cache[0]), .in_3(data_register_1_into_cache[1]),
    .in_4(data_register_1_into_cache[2]), .in_5(data_register_1_into_cache[3]),
    .in_6(data_register_1_into_cache[4]), .in_7(data_register_1_into_cache[5]),
    .in_8(data_register_1_into_cache[6]), .in_9(data_register_1_into_cache[7]),
    .out_10(n8_bit_condition_28_out_10), .out_11(n8_bit_condition_28_out_11),
    .out_12(n8_bit_condition_28_out_12), .out_13(n8_bit_condition_28_out_13),
    .out_14(n8_bit_condition_28_out_14), .out_15(n8_bit_condition_28_out_15),
    .out_16(n8_bit_condition_28_out_16), .out_17(n8_bit_condition_28_out_17),
    .Condition(select_byte_for_r_w_16_write));
  Byte Byte_12 (
    .in_3(n8_bit_condition_25_out_10), .in_4(n8_bit_condition_25_out_11), .in_5(n8_bit_condition_25_out_12),
    .in_6(n8_bit_condition_25_out_13), .in_7(n8_bit_condition_25_out_14), .in_8(n8_bit_condition_25_out_15),
    .in_9(n8_bit_condition_25_out_16), .in_10(n8_bit_condition_25_out_17), .out_11(Byte_12_out_11),
    .out_12(Byte_12_out_12), .out_13(Byte_12_out_13), .out_14(Byte_12_out_14), .out_15(Byte_12_out_15),
    .out_16(Byte_12_out_16), .out_17(Byte_12_out_17), .out_18(Byte_12_out_18),
    .R_W(select_byte_for_r_w_13_write), .Clock(Clock));
  _8_bit_Condition_Gate u_8_bit_condition_29 (
    .in_2(Byte_12_out_11), .in_3(Byte_12_out_12), .in_4(Byte_12_out_13), .in_5(Byte_12_out_14),
    .in_6(Byte_12_out_15), .in_7(Byte_12_out_16), .in_8(Byte_12_out_17), .in_9(Byte_12_out_18),
    .out_10(n8_bit_condition_29_out_10[0]), .out_11(n8_bit_condition_29_out_10[1]),
    .out_12(n8_bit_condition_29_out_10[2]), .out_13(n8_bit_condition_29_out_10[3]),
    .out_14(n8_bit_condition_29_out_10[4]), .out_15(n8_bit_condition_29_out_10[5]),
    .out_16(n8_bit_condition_29_out_10[6]), .out_17(n8_bit_condition_29_out_10[7]),
    .Condition(select_byte_for_r_w_13_read));
  _8_bit_Condition_Gate u_8_bit_condition_30 (
    .in_2(Byte_13_out_11), .in_3(Byte_13_out_12), .in_4(Byte_13_out_13), .in_5(Byte_13_out_14),
    .in_6(Byte_13_out_15), .in_7(Byte_13_out_16), .in_8(Byte_13_out_17), .in_9(Byte_13_out_18),
    .out_10(n8_bit_condition_30_out_10[0]), .out_11(n8_bit_condition_30_out_10[1]),
    .out_12(n8_bit_condition_30_out_10[2]), .out_13(n8_bit_condition_30_out_10[3]),
    .out_14(n8_bit_condition_30_out_10[4]), .out_15(n8_bit_condition_30_out_10[5]),
    .out_16(n8_bit_condition_30_out_10[6]), .out_17(n8_bit_condition_30_out_10[7]),
    .Condition(select_byte_for_r_w_14_read));
  Byte Byte_13 (
    .in_3(n8_bit_condition_26_out_10), .in_4(n8_bit_condition_26_out_11), .in_5(n8_bit_condition_26_out_12),
    .in_6(n8_bit_condition_26_out_13), .in_7(n8_bit_condition_26_out_14), .in_8(n8_bit_condition_26_out_15),
    .in_9(n8_bit_condition_26_out_16), .in_10(n8_bit_condition_26_out_17), .out_11(Byte_13_out_11),
    .out_12(Byte_13_out_12), .out_13(Byte_13_out_13), .out_14(Byte_13_out_14), .out_15(Byte_13_out_15),
    .out_16(Byte_13_out_16), .out_17(Byte_13_out_17), .out_18(Byte_13_out_18),
    .R_W(select_byte_for_r_w_14_write), .Clock(Clock));
  _8_bit_Condition_Gate u_8_bit_condition_31 (
    .in_2(Byte_14_out_11), .in_3(Byte_14_out_12), .in_4(Byte_14_out_13), .in_5(Byte_14_out_14),
    .in_6(Byte_14_out_15), .in_7(Byte_14_out_16), .in_8(Byte_14_out_17), .in_9(Byte_14_out_18),
    .out_10(n8_bit_condition_31_out_10[0]), .out_11(n8_bit_condition_31_out_10[1]),
    .out_12(n8_bit_condition_31_out_10[2]), .out_13(n8_bit_condition_31_out_10[3]),
    .out_14(n8_bit_condition_31_out_10[4]), .out_15(n8_bit_condition_31_out_10[5]),
    .out_16(n8_bit_condition_31_out_10[6]), .out_17(n8_bit_condition_31_out_10[7]),
    .Condition(select_byte_for_r_w_15_read));
  Byte Byte_14 (
    .in_3(n8_bit_condition_27_out_10), .in_4(n8_bit_condition_27_out_11), .in_5(n8_bit_condition_27_out_12),
    .in_6(n8_bit_condition_27_out_13), .in_7(n8_bit_condition_27_out_14), .in_8(n8_bit_condition_27_out_15),
    .in_9(n8_bit_condition_27_out_16), .in_10(n8_bit_condition_27_out_17), .out_11(Byte_14_out_11),
    .out_12(Byte_14_out_12), .out_13(Byte_14_out_13), .out_14(Byte_14_out_14), .out_15(Byte_14_out_15),
    .out_16(Byte_14_out_16), .out_17(Byte_14_out_17), .out_18(Byte_14_out_18),
    .R_W(select_byte_for_r_w_15_write), .Clock(Clock));
  _8_bit_Condition_Gate u_8_bit_condition_32 (
    .in_2(Byte_15_out_11), .in_3(Byte_15_out_12), .in_4(Byte_15_out_13), .in_5(Byte_15_out_14),
    .in_6(Byte_15_out_15), .in_7(Byte_15_out_16), .in_8(Byte_15_out_17), .in_9(Byte_15_out_18),
    .out_10(n8_bit_condition_32_out_10[0]), .out_11(n8_bit_condition_32_out_10[1]),
    .out_12(n8_bit_condition_32_out_10[2]), .out_13(n8_bit_condition_32_out_10[3]),
    .out_14(n8_bit_condition_32_out_10[4]), .out_15(n8_bit_condition_32_out_10[5]),
    .out_16(n8_bit_condition_32_out_10[6]), .out_17(n8_bit_condition_32_out_10[7]),
    .Condition(select_byte_for_r_w_16_read));
  Byte Byte_15 (
    .in_3(n8_bit_condition_28_out_10), .in_4(n8_bit_condition_28_out_11), .in_5(n8_bit_condition_28_out_12),
    .in_6(n8_bit_condition_28_out_13), .in_7(n8_bit_condition_28_out_14), .in_8(n8_bit_condition_28_out_15),
    .in_9(n8_bit_condition_28_out_16), .in_10(n8_bit_condition_28_out_17), .out_11(Byte_15_out_11),
    .out_12(Byte_15_out_12), .out_13(Byte_15_out_13), .out_14(Byte_15_out_14), .out_15(Byte_15_out_15),
    .out_16(Byte_15_out_16), .out_17(Byte_15_out_17), .out_18(Byte_15_out_18),
    .R_W(select_byte_for_r_w_16_write), .Clock(Clock));
  assign or_11_out = n8_bit_condition_29_out_10 | or_12_out;  // OR_Gate or_11, 8 bits wide
  assign or_12_out = n8_bit_condition_30_out_10 | or_13_out;  // OR_Gate or_12, 8 bits wide
  assign or_13_out = n8_bit_condition_31_out_10 | n8_bit_condition_32_out_10;  // OR_Gate or_13, 8 bits wide
endmodule

module Byte (
  input  R_W,
  input  Clock,
  input  in_3,
  input  in_4,
  input  in_5,
  input  in_6,
  input  in_7,
  input  in_8,
  input  in_9,
  input  in_10,
  output out_11,
  output out_12,
  output out_13,
  output out_14,
  output out_15,
  output out_16,
  output out_17,
  output out_18
);

  wire _0_q, _1_q, _2_q, _3_q, _4_q, _5_q, _6_q, _7_q, and_1_out, and_2_out, and_3_out, and_4_out, and_5_out,
       and_6_out, and_7_out, and_8_out, and_9_out, and_10_out, and_11_out, and_12_out, and_13_out,
       and_14_out, and_15_out, and_16_out, not_1_out, or_1_out, or_2_out, or_3_out, or_4_out, or_5_out,
       or_6_out, or_7_out, or_8_out;

  not not_1 (not_1_out, R_W);
  and and_1 (and_1_out, _0_q, not_1_out);
  or or_1 (or_1_out, and_1_out, and_2_out);
  and and_2 (and_2_out, R_W, in_3);
  and and_3 (and_3_out, _1_q, not_1_out);
  or or_2 (or_2_out, and_3_out, and_4_out);
  and and_4 (and_4_out, R_W, in_4);
  and and_5 (and_5_out, _2_q, not_1_out);
  or or_3 (or_3_out, and_5_out, and_6_out);
  and and_6 (and_6_out, R_W, in_5);
  and and_7 (and_7_out, _3_q, not_1_out);
  or or_4 (or_4_out, and_7_out, and_8_out);
  and and_8 (and_8_out, R_W, in_6);
  and and_9 (and_9_out, _4_q, not_1_out);
  or or_5 (or_5_out, and_9_out, and_10_out);
  and and_10 (and_10_out, R_W, in_7);
  and and_11 (and_11_out, _5_q, not_1_out);
  or or_6 (or_6_out, and_11_out, and_12_out);
  and and_12 (and_12_out, R_W, in_8);
  and and_13 (and_13_out, _6_q, not_1_out);
  or or_7 (or_7_out, and_13_out, and_14_out);
  and and_14 (and_14_out, R_W, in_9);
  and and_15 (and_15_out, _7_q, not_1_out);
  or or_8 (or_8_out, and_15_out, and_16_out);
  and and_16 (and_16_out, R_W, in_10);
  D_Flip_Flop _0 (.clk(Clock), .D(or_1_out), .Q(_0_q));  // open: Qn, preset, en, reset
  D_Flip_Flop _1 (.clk(Clock), .D(or_2_out), .Q(_1_q));  // open: Qn, preset, en, reset
  D_Flip_Flop _2 (.clk(Clock), .D(or_3_out), .Q(_2_q));  // open: Qn, preset, en, reset
  D_Flip_Flop _3 (.clk(Clock), .D(or_4_out), .Q(_3_q));  // open: Qn, preset, en, reset
  D_Flip_Flop _4 (.clk(Clock), .D(or_5_out), .Q(_4_q));  // open: Qn, preset, en, reset
  D_Flip_Flop _5 (.clk(Clock), .D(or_6_out), .Q(_5_q));  // open: Qn, preset, en, reset
  D_Flip_Flop _6 (.clk(Clock), .D(or_7_out), .Q(_6_q));  // open: Qn, preset, en, reset
  D_Flip_Flop _7 (.clk(Clock), .D(or_8_out), .Q(_7_q));  // open: Qn, preset, en, reset
  and and_17 (out_11, not_1_out, _0_q);
  and and_18 (out_12, not_1_out, _1_q);
  and and_19 (out_13, not_1_out, _2_q);
  and and_20 (out_14, not_1_out, _3_q);
  and and_21 (out_15, not_1_out, _4_q);
  and and_22 (out_16, not_1_out, _5_q);
  and and_23 (out_17, not_1_out, _6_q);
  and and_24 (out_18, not_1_out, _7_q);
endmodule

module _8_bit_Condition_Gate (
  input  Condition,
  input  in_2,
  input  in_3,
  input  in_4,
  input  in_5,
  input  in_6,
  input  in_7,
  input  in_8,
  input  in_9,
  output out_10,
  output out_11,
  output out_12,
  output out_13,
  output out_14,
  output out_15,
  output out_16,
  output out_17
);

  and _0 (out_10, in_2, Condition);
  and _1 (out_11, in_3, Condition);
  and _2 (out_12, in_4, Condition);
  and _3 (out_13, in_5, Condition);
  and _4 (out_14, in_6, Condition);
  and _5 (out_15, in_7, Condition);
  and _6 (out_16, in_8, Condition);
  and _7 (out_17, in_9, Condition);
endmodule

module Select_Byte_for_R_W (
  input  Selected,
  input  R_W,
  output Read,
  output Write
);

  wire not_1_out;

  not not_1 (not_1_out, R_W);
  and and_1 (Read, not_1_out, Selected);
  and and_2 (Write, R_W, Selected);
endmodule

module Data_Register (
  input  [7:0] External_Input,
  input  [7:0] from_Cache,
  input  R_W,
  input  Clock,
  output [7:0] External_Output,
  output [7:0] into_Cache
);

  wire and_1_out, and_2_out, and_5_out, and_6_out, and_9_out, and_12_out, and_15_out, and_16_out, and_17_out,
       and_18_out, and_19_out, and_20_out, and_21_out, and_22_out, and_25_out, and_26_out, d_ff_1_q,
       d_ff_2_q, d_ff_3_q, d_ff_4_q, d_ff_5_q, d_ff_6_q, d_ff_7_q, d_ff_8_q, not_1_out, not_2_out, or_1_out,
       or_2_out, or_3_out, or_4_out, or_5_out, or_6_out, or_7_out, or_8_out;

  not not_1 (not_1_out, R_W);
  and and_1 (and_1_out, R_W, from_Cache[7]);
  and and_2 (and_2_out, not_1_out, External_Input[7]);
  or or_1 (or_1_out, and_2_out, and_1_out);
  and and_3 (External_Output[6], R_W, d_ff_2_q);
  and and_4 (External_Output[7], R_W, d_ff_1_q);
  and and_5 (and_5_out, R_W, from_Cache[6]);
  and and_6 (and_6_out, not_1_out, External_Input[6]);
  or or_2 (or_2_out, and_6_out, and_5_out);
  D_Flip_Flop d_ff_1 (.clk(Clock), .D(or_1_out), .Q(d_ff_1_q));  // open: Qn, preset, en, reset
  not not_2 (not_2_out, R_W);
  and and_7 (External_Output[5], R_W, d_ff_3_q);
  and and_8 (External_Output[4], d_ff_4_q, R_W);
  and and_9 (and_9_out, not_1_out, External_Input[5]);
  D_Flip_Flop d_ff_2 (.clk(Clock), .D(or_2_out), .Q(d_ff_2_q));  // open: Qn, preset, en, reset
  and and_10 (External_Output[3], d_ff_5_q, R_W);
  and and_11 (External_Output[2], d_ff_6_q, R_W);
  and and_12 (and_12_out, R_W, from_Cache[5]);
  or or_3 (or_3_out, and_9_out, and_12_out);
  D_Flip_Flop d_ff_3 (.clk(Clock), .D(or_3_out), .Q(d_ff_3_q));  // open: Qn, preset, en, reset
  and and_13 (External_Output[1], d_ff_7_q, R_W);
  and and_14 (External_Output[0], d_ff_8_q, R_W);
  and and_15 (and_15_out, not_1_out, External_Input[4]);
  and and_16 (and_16_out, R_W, from_Cache[4]);
  or or_4 (or_4_out, and_15_out, and_16_out);
  D_Flip_Flop d_ff_4 (.clk(Clock), .D(or_4_out), .Q(d_ff_4_q));  // open: Qn, preset, en, reset
  and and_17 (and_17_out, not_1_out, External_Input[3]);
  and and_18 (and_18_out, R_W, from_Cache[3]);
  or or_5 (or_5_out, and_17_out, and_18_out);
  D_Flip_Flop d_ff_5 (.clk(Clock), .D(or_5_out), .Q(d_ff_5_q));  // open: Qn, preset, en, reset
  and and_19 (and_19_out, not_1_out, External_Input[2]);
  and and_20 (and_20_out, R_W, from_Cache[2]);
  or or_6 (or_6_out, and_19_out, and_20_out);
  D_Flip_Flop d_ff_6 (.clk(Clock), .D(or_6_out), .Q(d_ff_6_q));  // open: Qn, preset, en, reset
  and and_21 (and_21_out, not_1_out, External_Input[1]);
  and and_22 (and_22_out, R_W, from_Cache[1]);
  or or_7 (or_7_out, and_21_out, and_22_out);
  and and_23 (into_Cache[7], d_ff_1_q, not_2_out);
  and and_24 (into_Cache[6], d_ff_2_q, not_2_out);
  and and_25 (and_25_out, R_W, from_Cache[0]);
  and and_26 (and_26_out, not_1_out, External_Input[0]);
  or or_8 (or_8_out, and_26_out, and_25_out);
  D_Flip_Flop d_ff_7 (.clk(Clock), .D(or_7_out), .Q(d_ff_7_q));  // open: Qn, preset, en, reset
  and and_27 (into_Cache[5], d_ff_3_q, not_2_out);
  and and_28 (into_Cache[4], d_ff_4_q, not_2_out);
  D_Flip_Flop d_ff_8 (.clk(Clock), .D(or_8_out), .Q(d_ff_8_q));  // open: Qn, preset, en, reset
  and and_29 (into_Cache[3], d_ff_5_q, not_2_out);
  and and_30 (into_Cache[2], d_ff_6_q, not_2_out);
  and and_31 (into_Cache[0], d_ff_8_q, not_2_out);
  and and_32 (into_Cache[1], d_ff_7_q, not_2_out);

  // Notes on the sheet:
  //   R/W = 1: Write to Register From Cache/Output Externally
  //   R/W = 0: Read Data from Input/Write to Cache
endmodule
