// Logisim project PC.circ as structural Verilog: 2 circuits, main circuit main
module main (
  input  [3:0] in_1,
  input  in_2,
  input  in_3,
  output [3:0] out_4
);

  Register register_1 (
    .Read_0_or_Write_1(in_3), .Clock(in_2), .in_1(in_1[3]), .in_2(in_1[2]), .in_3(in_1[1]), .in_4(in_1[0]),
    .out_7(out_4[3]), .out_8(out_4[2]), .out_9(out_4[1]), .out_10(out_4[0]));
endmodule

module Register (
  input  in_1,
  input  in_2,
  input  in_3,
  input  in_4,
  input  Read_0_or_Write_1,
  input  Clock,
  output out_7,
  output out_8,
  output out_9,
  output out_10
);

  D_Flip_Flop d_ff_1 (.clk(Clock), .D(in_1), .Q(out_7), .en(Read_0_or_Write_1));  // open: Qn, preset, reset
  D_Flip_Flop d_ff_2 (.clk(Clock), .D(in_2), .Q(out_8), .en(Read_0_or_Write_1));  // open: Qn, preset, reset
  D_Flip_Flop d_ff_3 (.clk(Clock), .D(in_3), .Q(out_9), .en(Read_0_or_Write_1));  // open: Qn, preset, reset
  D_Flip_Flop d_ff_4 (.clk(Clock), .D(in_4), .Q(out_10), .en(Read_0_or_Write_1));  // open: Qn, preset, reset

  // Notes on the sheet:
  //   Read Input from RAM
endmodule
