// Logisim project REGISTER.circ as structural Verilog: 2 circuits, main circuit main
module main (
  input  [7:0] INPUT,
  input  CLOCK,
  input  R_W,
  output [7:0] out_4
);

  Register register_1 (
    .Read_0_or_Write_1(R_W), .Clock(CLOCK), .in_1(INPUT[7]), .in_2(INPUT[6]), .in_3(INPUT[5]),
    .in_4(INPUT[4]), .in_5(INPUT[3]), .in_6(INPUT[2]), .in_7(INPUT[1]), .in_8(INPUT[0]), .out_11(out_4[7]),
    .out_12(out_4[6]), .out_13(out_4[5]), .out_14(out_4[4]), .out_15(out_4[3]), .out_16(out_4[2]),
    .out_17(out_4[1]), .out_18(out_4[0]));
endmodule

module Register (
  input  in_1,
  input  in_2,
  input  in_3,
  input  in_4,
  input  in_5,
  input  in_6,
  input  in_7,
  input  in_8,
  input  Read_0_or_Write_1,
  input  Clock,
  output out_11,
  output out_12,
  output out_13,
  output out_14,
  output out_15,
  output out_16,
  output out_17,
  output out_18
);

  wire d_ff_1_q, d_ff_2_q, d_ff_3_q, d_ff_4_q, d_ff_5_q, d_ff_6_q, d_ff_7_q, d_ff_8_q, not_1_out;

  not not_1 (not_1_out, Read_0_or_Write_1);
  D_Flip_Flop d_ff_1 (.clk(Clock), .D(in_1), .Q(d_ff_1_q), .en(Read_0_or_Write_1));  // open: Qn, preset, reset
  and and_1 (out_11, not_1_out, d_ff_1_q);
  D_Flip_Flop d_ff_2 (.clk(Clock), .D(in_2), .Q(d_ff_2_q), .en(Read_0_or_Write_1));  // open: Qn, preset, reset
  and and_2 (out_12, not_1_out, d_ff_2_q);
  D_Flip_Flop d_ff_3 (.clk(Clock), .D(in_3), .Q(d_ff_3_q), .en(Read_0_or_Write_1));  // open: Qn, preset, reset
  and and_3 (out_13, not_1_out, d_ff_3_q);
  D_Flip_Flop d_ff_4 (.clk(Clock), .D(in_4), .Q(d_ff_4_q), .en(Read_0_or_Write_1));  // open: Qn, preset, reset
  and and_4 (out_14, not_1_out, d_ff_4_q);
  D_Flip_Flop d_ff_5 (.clk(Clock), .D(in_5), .Q(d_ff_5_q), .en(Read_0_or_Write_1));  // open: Qn, preset, reset
  and and_5 (out_15, not_1_out, d_ff_5_q);
  D_Flip_Flop d_ff_6 (.clk(Clock), .D(in_6), .Q(d_ff_6_q), .en(Read_0_or_Write_1));  // open: Qn, preset, reset
  and and_6 (out_16, not_1_out, d_ff_6_q);
  D_Flip_Flop d_ff_7 (.clk(Clock), .D(in_7), .Q(d_ff_7_q), .en(Read_0_or_Write_1));  // open: Qn, preset, reset
  and and_7 (out_17, not_1_out, d_ff_7_q);
  D_Flip_Flop d_ff_8 (.clk(Clock), .D(in_8), .Q(d_ff_8_q), .en(Read_0_or_Write_1));  // open: Qn, preset, reset
  and and_8 (out_18, not_1_out, d_ff_8_q);

  // Notes on the sheet:
  //   Read Input from RAM
endmodule
